// Logisim project 1.circ as structural Verilog: 1 circuit, main circuit introduction
module introduction (
  input  A,
  input  B,
  input  C,
  input  D,
  output f,
  output g
);

  wire and_1_out, and_2_out, and_3_out, and_4_out, and_5_out, and_6_out, and_7_out, not_1_out, not_2_out,
       not_3_out, not_4_out, not_5_out, not_6_out, not_7_out, not_8_out;

  not not_1 (not_1_out, B);
  not not_2 (not_2_out, D);
  not not_3 (not_3_out, A);
  not not_4 (not_4_out, D);
  not not_5 (not_5_out, B);
  not not_6 (not_6_out, D);
  not not_7 (not_7_out, B);
  not not_8 (not_8_out, D);
  and and_1 (and_1_out, A, C);
  and and_2 (and_2_out, not_1_out, D);
  and and_3 (and_3_out, C, not_2_out);
  and and_4 (and_4_out, not_3_out, not_4_out);
  and and_5 (and_5_out, A, not_5_out, not_6_out);
  and and_6 (and_6_out, not_7_out, C, not_8_out);
  and and_7 (and_7_out, A, B, C, D);
  or or_1 (f, and_1_out, and_2_out, and_3_out);
  or or_2 (g, and_4_out, and_5_out, and_6_out, and_7_out);
endmodule
