// Logisim project 2.circ as structural Verilog: 1 circuit, main circuit minterm
module minterm (
  input  [3:0] fourbitinput,
  output h
);

  wire not_1_out;

  not not_1 (not_1_out, fourbitinput[2]);
  and and_1 (h, fourbitinput[3], not_1_out, fourbitinput[1], fourbitinput[0]);
endmodule
