// Logisim project 3.circ as structural Verilog: 1 circuit, main circuit maxterm
module maxterm (
  input  [3:0] fourbitinput,
  output j
);

  wire not_1_out, not_2_out;

  not not_1 (not_1_out, fourbitinput[3]);
  not not_2 (not_2_out, fourbitinput[0]);
  or or_1 (j, not_1_out, fourbitinput[2], fourbitinput[1], not_2_out);
endmodule
