// Logisim project 4.circ as structural Verilog: 1 circuit, main circuit karnaugh
module karnaugh (
  input  [3:0] fourbitinput,
  output k
);

  wire and_1_out, and_2_out, and_3_out, and_4_out, and_5_out, not_1_out, not_2_out, not_3_out, not_4_out,
       not_5_out, not_6_out, not_7_out;

  not not_1 (not_1_out, fourbitinput[3]);
  not not_2 (not_2_out, fourbitinput[1]);
  not not_3 (not_3_out, fourbitinput[0]);
  not not_4 (not_4_out, fourbitinput[3]);
  not not_5 (not_5_out, fourbitinput[2]);
  not not_6 (not_6_out, fourbitinput[1]);
  not not_7 (not_7_out, fourbitinput[3]);
  and and_1 (and_1_out, not_1_out, not_2_out, not_3_out);
  and and_2 (and_2_out, not_4_out, fourbitinput[2], fourbitinput[1]);
  and and_3 (and_3_out, fourbitinput[3], not_5_out, fourbitinput[1]);
  and and_4 (and_4_out, fourbitinput[3], fourbitinput[2], not_6_out, fourbitinput[0]);
  and and_5 (and_5_out, not_7_out, fourbitinput[1], fourbitinput[0]);
  or or_1 (k, and_1_out, and_2_out, and_3_out, and_4_out, and_5_out);

  // Other names for the same wires on the sheet: D = fourbitinput[0]; C = fourbitinput[1]; B = fourbitinput[2];
  //   A = fourbitinput[3]
endmodule
