// Logisim project 1.circ as structural Verilog: 1 circuit, main circuit bitcounting
module bitcounting (
  input  [11:0] twelvebitinput,
  output [3:0] zeroes
);

  wire a0, a1, a2, a3, a4, a5, a6, a7, a8, a9, a10, a11, adder_1_cout, adder_1_out, adder_2_cout,
       adder_2_out, adder_3_cout, adder_3_out, adder_4_cout, adder_4_out, adder_5_cout, adder_5_out,
       adder_6_cout, adder_6_out, adder_7_cout, adder_8_cout, adder_8_out, adder_9_cout, adder_9_out,
       adder_10_cout, adder_10_out, adder_11_cout, adder_11_out, adder_12_cout, adder_12_out, adder_13_cout,
       adder_14_cout, adder_14_out, adder_15_cout;

  Adder #(.width(1)) adder_1 (.a(a0), .b(a1), .out(adder_1_out), .cin(a2), .cout(adder_1_cout));
  Adder #(.width(1)) adder_2 (.a(a3), .b(a4), .out(adder_2_out), .cin(a5), .cout(adder_2_cout));
  Adder #(.width(1)) adder_3 (.a(a6), .b(a7), .out(adder_3_out), .cin(a8), .cout(adder_3_cout));
  Adder #(.width(1)) adder_4 (.a(a9), .b(a10), .out(adder_4_out), .cin(a11), .cout(adder_4_cout));
  assign {a11, a10, a9, a8, a7, a6, a5, a4, a3, a2, a1, a0} = ~twelvebitinput;  // NOT_Gate not_1, 12 bits wide
  Adder #(.width(1)) adder_5 (.a(adder_1_out), .b(adder_2_out), .out(adder_5_out), .cout(adder_5_cout));  // open: cin
  Adder #(.width(1)) adder_6 (.a(adder_1_cout), .b(adder_2_cout), .out(adder_6_out), .cout(adder_6_cout));  // open: cin
  Adder #(.width(1)) adder_7 (.a(adder_5_out), .b(adder_9_out), .out(zeroes[0]), .cout(adder_7_cout));  // open: cin
  Adder #(.width(1)) adder_8 (.a(adder_3_cout), .b(adder_4_cout), .out(adder_8_out), .cout(adder_8_cout));  // open: cin
  Adder #(.width(1)) adder_9 (.a(adder_3_out), .b(adder_4_out), .out(adder_9_out), .cout(adder_9_cout));  // open: cin
  Adder #(.width(1)) adder_10 (
    .a(adder_5_cout), .b(adder_9_cout), .out(adder_10_out), .cin(adder_7_cout), .cout(adder_10_cout));
  Adder #(.width(1)) adder_11 (
    .a(adder_6_out), .b(adder_8_out), .out(adder_11_out), .cout(adder_11_cout));  // open: cin
  Adder #(.width(1)) adder_12 (
    .a(adder_6_cout), .b(adder_8_cout), .out(adder_12_out), .cout(adder_12_cout));  // open: cin
  Adder #(.width(1)) adder_13 (.a(adder_10_out), .b(adder_11_out), .out(zeroes[1]), .cout(adder_13_cout));  // open: cin
  Adder #(.width(1)) adder_14 (
    .a(adder_10_cout), .b(adder_11_cout), .out(adder_14_out), .cin(adder_13_cout), .cout(adder_14_cout));
  Adder #(.width(1)) adder_15 (.a(adder_14_out), .b(adder_12_out), .out(zeroes[2]), .cout(adder_15_cout));  // open: cin
  Adder #(.width(1)) adder_16 (
    .a(adder_14_cout), .b(adder_12_cout), .out(zeroes[3]), .cin(adder_15_cout));  // open: cout

  // Other names for the same wires on the sheet: z0 = zeroes[0]; z1 = zeroes[1]; z2 = zeroes[2]; z3 = zeroes[3]
endmodule
