// Logisim project 2.circ as structural Verilog: 1 circuit, main circuit comparison
module comparison (
  input  [1:0] inputa,
  input  [1:0] inputb,
  output areequal,
  output greaterthan,
  output lessthan
);

  wire an0, an1, bn0, bn1, g1, g2, g3, l1, l2, l3, nand_9_out;

  nand nand_1 (an1, inputa[1], inputa[1]);
  nand nand_2 (an0, inputa[0], inputa[0]);
  nand nand_3 (bn1, inputb[1], inputb[1]);
  nand nand_4 (bn0, inputb[0], inputb[0]);
  nand nand_5 (g1, inputa[0], bn1, bn0);
  nand nand_6 (g2, inputa[1], inputa[0], bn0);
  nand nand_7 (g3, inputa[1], bn1);
  nand nand_8 (greaterthan, g1, g2, g3);
  nand nand_9 (nand_9_out, g1, g2, g3, l1, l2, l3);
  nand nand_10 (l1, an1, an0, inputb[0]);
  nand nand_11 (l2, an0, inputb[1], inputb[0]);
  nand nand_12 (l3, an1, inputb[1]);
  nand nand_13 (areequal, nand_9_out, nand_9_out);
  nand nand_14 (lessthan, l1, l2, l3);

  // Other names for the same wires on the sheet: e = areequal; g = greaterthan; a0 = inputa[0]; a1 = inputa[1];
  //   b0 = inputb[0]; b1 = inputb[1]; l = lessthan
endmodule
