// Logisim project 3.circ as structural Verilog: 1 circuit, main circuit parity
module parity (
  input  [9:0] tenbitinput,
  output [10:0] evenparity
);

  wire xor_1_out, xor_2_out, xor_3_out, xor_4_out, xor_5_out, xor_6_out, xor_7_out, xor_8_out;

  xor xor_1 (xor_1_out, tenbitinput[0], tenbitinput[1]);
  xor xor_2 (xor_2_out, xor_1_out, tenbitinput[2]);
  xor xor_3 (xor_3_out, xor_2_out, tenbitinput[3]);
  xor xor_4 (xor_4_out, xor_3_out, tenbitinput[4]);
  xor xor_5 (xor_5_out, xor_4_out, tenbitinput[5]);
  xor xor_6 (xor_6_out, xor_5_out, tenbitinput[6]);
  xor xor_7 (xor_7_out, xor_6_out, tenbitinput[7]);
  xor xor_8 (xor_8_out, xor_7_out, tenbitinput[8]);
  xor xor_9 (evenparity[0], xor_8_out, tenbitinput[9]);

  assign evenparity[10:1] = tenbitinput;

  // Other names for the same wires on the sheet: ep[10:0] = {tenbitinput, evenparity[0]}; j = tenbitinput[0];
  //   i = tenbitinput[1]; h = tenbitinput[2]; g = tenbitinput[3]; f = tenbitinput[4]; e = tenbitinput[5];
  //   d = tenbitinput[6]; c = tenbitinput[7]; b = tenbitinput[8]; a = tenbitinput[9]
endmodule
