// Logisim project 4.circ as structural Verilog: 1 circuit, main circuit cla
module cla (
  input  [5:0] inputa,
  input  [5:0] inputb,
  input  carryin,
  output [5:0] carryout,
  output [5:0] generator,
  output [5:0] propagator
);

  wire and_7_out, and_8_out, and_9_out, and_10_out, and_11_out, and_12_out, and_13_out, and_14_out,
       and_15_out, and_16_out, and_17_out, and_18_out, and_19_out, and_20_out, and_21_out, and_22_out,
       and_23_out, and_24_out, and_25_out, and_26_out, and_27_out;

  and and_1 (generator[0], inputa[0], inputb[0]);
  xor xor_1 (propagator[0], inputa[0], inputb[0]);
  and and_2 (generator[1], inputa[1], inputb[1]);
  xor xor_2 (propagator[1], inputa[1], inputb[1]);
  and and_3 (generator[2], inputa[2], inputb[2]);
  xor xor_3 (propagator[2], inputa[2], inputb[2]);
  and and_4 (generator[3], inputa[3], inputb[3]);
  xor xor_4 (propagator[3], inputa[3], inputb[3]);
  and and_5 (generator[4], inputa[4], inputb[4]);
  xor xor_5 (propagator[4], inputa[4], inputb[4]);
  and and_6 (generator[5], inputa[5], inputb[5]);
  xor xor_6 (propagator[5], inputa[5], inputb[5]);
  and and_7 (and_7_out, propagator[0], carryin);
  and and_8 (and_8_out, propagator[0], propagator[1], carryin);
  and and_9 (and_9_out, propagator[1], generator[0]);
  and and_10 (and_10_out, propagator[2], propagator[0], propagator[1], carryin);
  and and_11 (and_11_out, propagator[2], propagator[1], generator[0]);
  and and_12 (and_12_out, propagator[2], generator[1]);
  and and_13 (and_13_out, propagator[3], propagator[2], propagator[0], propagator[1], carryin);
  and and_14 (and_14_out, propagator[3], propagator[2], propagator[1], generator[0]);
  and and_15 (and_15_out, propagator[3], propagator[2], generator[1]);
  and and_16 (and_16_out, propagator[3], generator[2]);
  or or_1 (carryout[0], and_7_out, generator[0]);
  or or_2 (carryout[1], and_8_out, and_9_out, generator[1]);
  or or_3 (carryout[2], and_10_out, and_11_out, and_12_out, generator[2]);
  or or_4 (carryout[3], and_13_out, and_14_out, and_15_out, and_16_out, generator[3]);
  and and_17 (and_17_out, propagator[4], propagator[3], propagator[2], propagator[0], propagator[1], carryin);
  and and_18 (and_18_out, propagator[4], propagator[3], propagator[2], propagator[1], generator[0]);
  and and_19 (and_19_out, propagator[4], propagator[3], propagator[2], generator[1]);
  and and_20 (and_20_out, propagator[4], propagator[3], generator[2]);
  and and_21 (and_21_out, propagator[4], generator[3]);
  and and_22 (and_22_out, propagator[5], propagator[4], propagator[3], propagator[2], propagator[0], propagator[1], carryin);
  and and_23 (and_23_out, propagator[5], propagator[4], propagator[3], propagator[2], propagator[1], generator[0]);
  and and_24 (and_24_out, propagator[5], propagator[4], propagator[3], propagator[2], generator[1]);
  and and_25 (and_25_out, propagator[5], propagator[4], propagator[3], generator[2]);
  and and_26 (and_26_out, propagator[5], propagator[4], generator[3]);
  and and_27 (and_27_out, propagator[5], generator[4]);
  or or_5 (carryout[4], and_17_out, and_18_out, and_19_out, and_20_out, and_21_out, generator[4]);
  or or_6 (carryout[5], and_22_out, and_23_out, and_24_out, and_25_out, and_26_out, and_27_out, generator[5]);

  // Other names for the same wires on the sheet: ci = carryin; C0 = carryout[0]; co[5:0] = carryout; C1 = carryout[1];
  //   C2 = carryout[2]; C3 = carryout[3]; C4 = carryout[4]; C5 = carryout[5]; g[5:0] = generator; G0 = generator[0];
  //   G1 = generator[1]; G2 = generator[2]; G3 = generator[3]; G4 = generator[4]; G5 = generator[5]; a0 = inputa[0];
  //   a1 = inputa[1]; a2 = inputa[2]; a3 = inputa[3]; a4 = inputa[4]; a5 = inputa[5]; b0 = inputb[0]; b1 = inputb[1];
  //   b2 = inputb[2]; b3 = inputb[3]; b4 = inputb[4]; b5 = inputb[5]; p[5:0] = propagator; P0 = propagator[0];
  //   P1 = propagator[1]; P2 = propagator[2]; P3 = propagator[3]; P4 = propagator[4]; P5 = propagator[5]
endmodule
