// Logisim project 5.circ as structural Verilog: 1 circuit, main circuit alu
module alu (
  input  [11:0] inputa,
  input  [11:0] inputb,
  input  [2:0] operation,
  output [11:0] aluout,
  output overflow,
  output carry,
  output zero
);

  wire and0, and1, and2, and3, and4, and5, and6, and7, and8, and9, and10, and11, and_13_out, and_14_out,
       and_15_out, and_16_out, and_17_out, and_18_out, and_19_out, and_20_out, and_21_out, and_22_out,
       and_23_out, and_24_out, and_25_out, and_26_out, and_27_out, and_28_out, and_29_out, and_30_out,
       and_31_out, and_32_out, and_33_out, and_34_out, and_35_out, and_36_out, and_37_out, and_38_out,
       and_39_out, and_40_out, and_41_out, and_42_out, and_43_out, and_44_out, and_45_out, and_46_out,
       and_47_out, and_48_out, and_50_out, and_51_out, and_52_out, and_53_out, and_54_out, and_55_out,
       and_56_out, and_57_out, and_58_out, and_59_out, and_62_out, and_63_out, and_64_out, and_65_out,
       and_66_out, and_67_out, and_68_out, and_69_out, and_70_out, and_71_out, c0, c1, c2, c3, c4, c5, c6,
       c7, c8, c9, c10, c11, ci611, cout, coutadd, coutdec, coutinc, coutsub, dec0, dec1, dec2, dec3, dec4,
       dec5, dec6, dec7, dec8, dec9, dec10, dec11, g0, g1, g2, g3, g4, g5, g6, g7, g8, g9, g10, g11, inc0,
       inc1, inc2, inc3, inc4, inc5, inc6, inc7, inc8, inc9, inc10, inc11, not0, not1, not2, not3, not4,
       not5, not6, not7, not8, not9, not10, not11, not_1_out, not_2_out, not_3_out, not_4_out, not_5_out,
       not_6_out, not_7_out, not_8_out, not_9_out, not_10_out, not_11_out, not_12_out, not_13_out,
       not_14_out, not_15_out, not_16_out, not_17_out, not_18_out, not_19_out, not_20_out, not_21_out,
       not_22_out, not_23_out, not_24_out, not_25_out, not_26_out, not_27_out, not_28_out, not_29_out,
       not_30_out, not_31_out, not_32_out, not_33_out, not_34_out, not_35_out, not_36_out, not_37_out,
       not_38_out, not_39_out, not_40_out, not_41_out, not_42_out, not_43_out, not_44_out, not_45_out,
       not_46_out, not_47_out, not_48_out, not_49_out, not_50_out, or0, or1, or2, or3, or4, or5, or6, or7,
       or8, or9, or10, or11, or_1_out, or_2_out, or_3_out, or_4_out, or_5_out, or_7_out, or_8_out, or_9_out,
       or_10_out, or_13_out, or_14_out, or_15_out, or_16_out, or_17_out, or_18_out, or_19_out, or_20_out,
       or_21_out, or_22_out, ovfadd, ovfdec, ovfinc, ovfsub, p0, p1, p2, p3, p4, p5, p6, p7, p8, p9, p10,
       p11, padd, pdec, pinc, psub, sub0, sub1, sub2, sub3, sub4, sub5, sub6, sub7, sub8, sub9, sub10, sub11,
       xor_1_out, xor_2_out, xor_3_out, xor_4_out, xor_5_out, xor_6_out, xor_7_out, xor_8_out, xor_9_out,
       xor_10_out, xor_11_out, xor_12_out;
  wire [11:0] adds;

  and and_1 (and0, inputa[0], inputb[0]);
  and and_2 (and1, inputa[1], inputb[1]);
  and and_3 (and2, inputa[2], inputb[2]);
  and and_4 (and3, inputa[3], inputb[3]);
  and and_5 (and4, inputa[4], inputb[4]);
  and and_6 (and5, inputa[5], inputb[5]);
  and and_7 (and6, inputa[6], inputb[6]);
  and and_8 (and7, inputa[7], inputb[7]);
  and and_9 (and8, inputa[8], inputb[8]);
  and and_10 (and9, inputa[9], inputb[9]);
  and and_11 (and10, inputa[10], inputb[10]);
  and and_12 (and11, inputa[11], inputb[11]);
  not not_1 (not_1_out, inputa[0]);
  not not_2 (not_2_out, inputa[1]);
  not not_3 (not_3_out, inputa[2]);
  not not_4 (not_4_out, inputa[3]);
  not not_5 (not_5_out, inputa[4]);
  not not_6 (not_6_out, inputa[5]);
  not not_7 (not_7_out, inputa[6]);
  not not_8 (not_8_out, inputa[7]);
  not not_9 (not_9_out, inputa[8]);
  not not_10 (not_10_out, inputa[9]);
  not not_11 (not_11_out, inputa[10]);
  not not_12 (not_12_out, inputa[11]);
  and and_13 (and_13_out, 1'b0, p0);
  and and_14 (and_14_out, or_1_out, p1);
  and and_15 (and_15_out, or_2_out, p2);
  and and_16 (and_16_out, or_3_out, p3);
  and and_17 (and_17_out, or_4_out, p4);
  and and_18 (and_18_out, or_5_out, p5);
  and and_19 (and_19_out, ci611, p6);
  and and_20 (and_20_out, or_7_out, p7);
  and and_21 (and_21_out, or_8_out, p8);
  and and_22 (and_22_out, or_9_out, p9);
  and and_23 (and_23_out, or_10_out, p10);
  and and_24 (and_24_out, padd, p11);
  xor xor_1 (xor_1_out, inputa[0], inputb[0]);
  and and_25 (and_25_out, inputb[0], not_1_out);
  xor xor_2 (xor_2_out, inputa[1], inputb[1]);
  and and_26 (and_26_out, inputb[1], not_2_out);
  xor xor_3 (xor_3_out, inputa[2], inputb[2]);
  and and_27 (and_27_out, inputb[2], not_3_out);
  xor xor_4 (xor_4_out, inputa[3], inputb[3]);
  and and_28 (and_28_out, inputb[3], not_4_out);
  xor xor_5 (xor_5_out, inputa[4], inputb[4]);
  and and_29 (and_29_out, inputb[4], not_5_out);
  xor xor_6 (xor_6_out, inputa[5], inputb[5]);
  and and_30 (and_30_out, inputb[5], not_6_out);
  xor xor_7 (xor_7_out, inputa[6], inputb[6]);
  and and_31 (and_31_out, inputb[6], not_7_out);
  xor xor_8 (xor_8_out, inputa[7], inputb[7]);
  and and_32 (and_32_out, inputb[7], not_8_out);
  xor xor_9 (xor_9_out, inputa[8], inputb[8]);
  and and_33 (and_33_out, inputb[8], not_9_out);
  xor xor_10 (xor_10_out, inputa[9], inputb[9]);
  and and_34 (and_34_out, inputb[9], not_10_out);
  xor xor_11 (xor_11_out, inputa[10], inputb[10]);
  and and_35 (and_35_out, inputb[10], not_11_out);
  xor xor_12 (xor_12_out, inputa[11], inputb[11]);
  and and_36 (and_36_out, inputb[11], not_12_out);
  xor xor_13 (ovfadd, padd, coutadd);
  xor xor_14 (ovfsub, psub, coutsub);
  xor xor_15 (ovfinc, pinc, coutinc);
  xor xor_16 (ovfdec, pdec, coutdec);
  Multiplexer #(.enable("false")) multiplexer_1 (.in0(1'b0), .in1(cout), .out(carry), .sel(operation[2]));
  not not_13 (not_13_out, xor_1_out);
  not not_14 (not_14_out, xor_2_out);
  not not_15 (not_15_out, xor_3_out);
  not not_16 (not_16_out, xor_4_out);
  not not_17 (not_17_out, xor_5_out);
  not not_18 (not_18_out, xor_6_out);
  not not_19 (not_19_out, xor_7_out);
  not not_20 (not_20_out, xor_8_out);
  not not_21 (not_21_out, xor_9_out);
  not not_22 (not_22_out, xor_10_out);
  not not_23 (not_23_out, xor_11_out);
  not not_24 (not_24_out, xor_12_out);
  not not_25 (not_25_out, aluout[0]);
  not not_26 (not_26_out, aluout[1]);
  not not_27 (not_27_out, aluout[2]);
  not not_28 (not_28_out, aluout[3]);
  not not_29 (not_29_out, aluout[4]);
  not not_30 (not_30_out, aluout[5]);
  not not_31 (not_31_out, aluout[6]);
  not not_32 (not_32_out, aluout[7]);
  not not_33 (not_33_out, aluout[8]);
  not not_34 (not_34_out, aluout[9]);
  not not_35 (not_35_out, aluout[10]);
  not not_36 (not_36_out, aluout[11]);
  or or_1 (or_1_out, g0, and_13_out);
  or or_2 (or_2_out, g1, and_14_out);
  or or_3 (or_3_out, g2, and_15_out);
  or or_4 (or_4_out, g3, and_16_out);
  or or_5 (or_5_out, g4, and_17_out);
  or or_6 (ci611, g5, and_18_out);
  or or_7 (or_7_out, g6, and_19_out);
  or or_8 (or_8_out, g7, and_20_out);
  or or_9 (or_9_out, g8, and_21_out);
  or or_10 (or_10_out, g9, and_22_out);
  or or_11 (padd, g10, and_23_out);
  or or_12 (coutadd, g11, and_24_out);
  xor xor_17 (sub0, xor_1_out, 1'b0);
  and and_37 (and_37_out, 1'b0, not_13_out);
  xor xor_18 (sub1, xor_2_out, or_13_out);
  and and_38 (and_38_out, or_13_out, not_14_out);
  xor xor_19 (sub2, xor_3_out, or_14_out);
  and and_39 (and_39_out, or_14_out, not_15_out);
  xor xor_20 (sub3, xor_4_out, or_15_out);
  and and_40 (and_40_out, or_15_out, not_16_out);
  xor xor_21 (sub4, xor_5_out, or_16_out);
  and and_41 (and_41_out, or_16_out, not_17_out);
  xor xor_22 (sub5, xor_6_out, or_17_out);
  and and_42 (and_42_out, or_17_out, not_18_out);
  xor xor_23 (sub6, xor_7_out, or_18_out);
  and and_43 (and_43_out, or_18_out, not_19_out);
  xor xor_24 (sub7, xor_8_out, or_19_out);
  and and_44 (and_44_out, or_19_out, not_20_out);
  xor xor_25 (sub8, xor_9_out, or_20_out);
  and and_45 (and_45_out, or_20_out, not_21_out);
  xor xor_26 (sub9, xor_10_out, or_21_out);
  and and_46 (and_46_out, or_21_out, not_22_out);
  xor xor_27 (sub10, xor_11_out, or_22_out);
  and and_47 (and_47_out, or_22_out, not_23_out);
  xor xor_28 (sub11, xor_12_out, psub);
  and and_48 (and_48_out, psub, not_24_out);
  cla cla_1 (
    .inputa(inputa[5:0]), .inputb(inputb[5:0]), .carryin(1'b0), .carryout({c5, c4, c3, c2, c1, c0}),
    .generator({g5, g4, g3, g2, g1, g0}), .propagator({p5, p4, p3, p2, p1, p0}));
  cla cla_2 (
    .inputa(inputa[11:6]), .inputb(inputb[11:6]), .carryin(ci611), .carryout({c11, c10, c9, c8, c7, c6}),
    .generator({g11, g10, g9, g8, g7, g6}), .propagator({p11, p10, p9, p8, p7, p6}));
  or or_13 (or_13_out, and_37_out, and_25_out);
  or or_14 (or_14_out, and_38_out, and_26_out);
  or or_15 (or_15_out, and_39_out, and_27_out);
  or or_16 (or_16_out, and_40_out, and_28_out);
  or or_17 (or_17_out, and_41_out, and_29_out);
  or or_18 (or_18_out, and_42_out, and_30_out);
  or or_19 (or_19_out, and_43_out, and_31_out);
  or or_20 (or_20_out, and_44_out, and_32_out);
  or or_21 (or_21_out, and_45_out, and_33_out);
  or or_22 (or_22_out, and_46_out, and_34_out);
  or or_23 (psub, and_47_out, and_35_out);
  or or_24 (coutsub, and_48_out, and_36_out);
  and and_49 (zero, not_25_out, not_26_out, not_27_out, not_28_out, not_29_out, not_30_out, not_31_out, not_32_out, not_33_out, not_34_out, not_35_out, not_36_out);
  xor xor_29 (adds[0], 1'b0, p0);
  xor xor_30 (adds[1], or_1_out, p1);
  xor xor_31 (adds[2], or_2_out, p2);
  xor xor_32 (adds[3], or_3_out, p3);
  xor xor_33 (adds[4], or_4_out, p4);
  xor xor_34 (adds[5], or_5_out, p5);
  xor xor_35 (adds[6], ci611, p6);
  xor xor_36 (adds[7], or_7_out, p7);
  xor xor_37 (adds[8], or_8_out, p8);
  xor xor_38 (adds[9], or_9_out, p9);
  xor xor_39 (adds[10], or_10_out, p10);
  xor xor_40 (adds[11], padd, p11);
  or or_25 (or0, inputa[0], inputb[0]);
  or or_26 (or1, inputa[1], inputb[1]);
  or or_27 (or2, inputa[2], inputb[2]);
  or or_28 (or3, inputa[3], inputb[3]);
  or or_29 (or4, inputa[4], inputb[4]);
  or or_30 (or5, inputa[5], inputb[5]);
  or or_31 (or6, inputa[6], inputb[6]);
  or or_32 (or7, inputa[7], inputb[7]);
  or or_33 (or8, inputa[8], inputb[8]);
  or or_34 (or9, inputa[9], inputb[9]);
  or or_35 (or10, inputa[10], inputb[10]);
  or or_36 (or11, inputa[11], inputb[11]);
  not not_37 (not_37_out, inputa[0]);
  not not_38 (not_38_out, inputa[1]);
  not not_39 (not_39_out, inputa[2]);
  not not_40 (not_40_out, inputa[3]);
  not not_41 (not_41_out, inputa[4]);
  not not_42 (not_42_out, inputa[5]);
  not not_43 (not_43_out, inputa[6]);
  not not_44 (not_44_out, inputa[7]);
  not not_45 (not_45_out, inputa[8]);
  not not_46 (not_46_out, inputa[9]);
  not not_47 (not_47_out, inputa[10]);
  not not_48 (not_48_out, inputa[11]);
  xor xor_41 (dec0, inputa[0], 1'b1);
  and and_50 (and_50_out, not_37_out, 1'b1);
  xor xor_42 (dec1, inputa[1], and_50_out);
  and and_51 (and_51_out, not_38_out, and_50_out);
  xor xor_43 (dec2, inputa[2], and_51_out);
  and and_52 (and_52_out, not_39_out, and_51_out);
  xor xor_44 (dec3, inputa[3], and_52_out);
  and and_53 (and_53_out, not_40_out, and_52_out);
  xor xor_45 (dec4, inputa[4], and_53_out);
  and and_54 (and_54_out, not_41_out, and_53_out);
  xor xor_46 (dec5, inputa[5], and_54_out);
  and and_55 (and_55_out, not_42_out, and_54_out);
  xor xor_47 (dec6, inputa[6], and_55_out);
  and and_56 (and_56_out, not_43_out, and_55_out);
  xor xor_48 (dec7, inputa[7], and_56_out);
  and and_57 (and_57_out, not_44_out, and_56_out);
  xor xor_49 (dec8, inputa[8], and_57_out);
  and and_58 (and_58_out, not_45_out, and_57_out);
  xor xor_50 (dec9, inputa[9], and_58_out);
  and and_59 (and_59_out, not_46_out, and_58_out);
  xor xor_51 (dec10, inputa[10], and_59_out);
  and and_60 (pdec, not_47_out, and_59_out);
  xor xor_52 (dec11, inputa[11], pdec);
  and and_61 (coutdec, not_48_out, pdec);
  Multiplexer #(.select(3), .width(12), .enable("false")) multiplexer_2 (
    .in0({and11, and10, and9, and8, and7, and6, and5, and4, and3, and2, and1, and0}),
    .in1({or11, or10, or9, or8, or7, or6, or5, or4, or3, or2, or1, or0}),
    .in2({p11, p10, p9, p8, p7, p6, p5, p4, p3, p2, p1, p0}),
    .in3({not11, not10, not9, not8, not7, not6, not5, not4, not3, not2, not1, not0}), .in4(adds),
    .in5({sub11, sub10, sub9, sub8, sub7, sub6, sub5, sub4, sub3, sub2, sub1, sub0}),
    .in6({inc11, inc10, inc9, inc8, inc7, inc6, inc5, inc4, inc3, inc2, inc1, inc0}),
    .in7({dec11, dec10, dec9, dec8, dec7, dec6, dec5, dec4, dec3, dec2, dec1, dec0}), .out(aluout),
    .sel(operation));
  xor xor_53 (inc0, inputa[0], 1'b1);
  and and_62 (and_62_out, inputa[0], inputa[0]);
  xor xor_54 (inc1, and_62_out, inputa[1]);
  and and_63 (and_63_out, and_62_out, inputa[1]);
  xor xor_55 (inc2, and_63_out, inputa[2]);
  and and_64 (and_64_out, and_63_out, inputa[2]);
  xor xor_56 (inc3, and_64_out, inputa[3]);
  and and_65 (and_65_out, and_64_out, inputa[3]);
  xor xor_57 (inc4, and_65_out, inputa[4]);
  and and_66 (and_66_out, and_65_out, inputa[4]);
  xor xor_58 (inc5, and_66_out, inputa[5]);
  and and_67 (and_67_out, and_66_out, inputa[5]);
  xor xor_59 (inc6, and_67_out, inputa[6]);
  and and_68 (and_68_out, and_67_out, inputa[6]);
  xor xor_60 (inc7, and_68_out, inputa[7]);
  and and_69 (and_69_out, and_68_out, inputa[7]);
  xor xor_61 (inc8, and_69_out, inputa[8]);
  and and_70 (and_70_out, and_69_out, inputa[8]);
  xor xor_62 (inc9, and_70_out, inputa[9]);
  and and_71 (and_71_out, and_70_out, inputa[9]);
  xor xor_63 (inc10, and_71_out, inputa[10]);
  and and_72 (pinc, and_71_out, inputa[10]);
  xor xor_64 (inc11, pinc, inputa[11]);
  and and_73 (coutinc, pinc, inputa[11]);
  xor xor_65 (not0, inputa[0], 1'b1);
  xor xor_66 (not1, inputa[1], 1'b1);
  xor xor_67 (not2, inputa[2], 1'b1);
  xor xor_68 (not3, inputa[3], 1'b1);
  xor xor_69 (not4, inputa[4], 1'b1);
  xor xor_70 (not5, inputa[5], 1'b1);
  xor xor_71 (not6, inputa[6], 1'b1);
  xor xor_72 (not7, inputa[7], 1'b1);
  xor xor_73 (not8, inputa[8], 1'b1);
  xor xor_74 (not9, inputa[9], 1'b1);
  xor xor_75 (not10, inputa[10], 1'b1);
  xor xor_76 (not11, inputa[11], 1'b1);
  not not_49 (not_49_out, coutsub);
  not not_50 (not_50_out, coutdec);
  Multiplexer #(.select(3), .enable("false")) multiplexer_3 (
    .in0(1'b0), .in1(1'b0), .in2(1'b0), .in3(1'b0), .in4(coutadd), .in5(not_49_out), .in6(coutinc),
    .in7(not_50_out), .out(cout), .sel(operation));
  Multiplexer #(.select(3), .enable("false")) multiplexer_4 (
    .in0(1'b0), .in1(1'b0), .in2(1'b0), .in3(1'b0), .in4(ovfadd), .in5(ovfsub), .in6(ovfinc), .in7(ovfdec),
    .out(overflow), .sel(operation));

  // Other names for the same wires on the sheet: xors[11:0] = {p11, p10, p9, p8, p7, p6, p5, p4, p3, p2, p1, p0};
  //   a[11:0] = inputa; a0 = inputa[0]; a1 = inputa[1]; a2 = inputa[2]; a3 = inputa[3]; a4 = inputa[4];
  //   a5 = inputa[5]; a6 = inputa[6]; a7 = inputa[7]; a8 = inputa[8]; a9 = inputa[9]; a10 = inputa[10];
  //   a11 = inputa[11]; s0 = adds[0]; s1 = adds[1]; s2 = adds[2]; s3 = adds[3]; s4 = adds[4]; s5 = adds[5];
  //   s6 = adds[6]; s7 = adds[7]; s8 = adds[8]; s9 = adds[9]; s10 = adds[10]; s11 = adds[11]; alu[11:0] = aluout;
  //   o0 = aluout[0]; o1 = aluout[1]; o2 = aluout[2]; o3 = aluout[3]; o4 = aluout[4]; o5 = aluout[5]; o6 = aluout[6];
  //   o7 = aluout[7]; o8 = aluout[8]; o9 = aluout[9]; o10 = aluout[10]; o11 = aluout[11];
  //   ands[11:0] = {and11, and10, and9, and8, and7, and6, and5, and4, and3, and2, and1, and0}; b[11:0] = inputb;
  //   b0 = inputb[0]; b1 = inputb[1]; b2 = inputb[2]; b3 = inputb[3]; b4 = inputb[4]; b5 = inputb[5]; b6 = inputb[6];
  //   b7 = inputb[7]; b8 = inputb[8]; b9 = inputb[9]; b10 = inputb[10]; b11 = inputb[11];
  //   decs[11:0] = {dec11, dec10, dec9, dec8, dec7, dec6, dec5, dec4, dec3, dec2, dec1, dec0};
  //   incs[11:0] = {inc11, inc10, inc9, inc8, inc7, inc6, inc5, inc4, inc3, inc2, inc1, inc0};
  //   nots[11:0] = {not11, not10, not9, not8, not7, not6, not5, not4, not3, not2, not1, not0}; op[2:0] = operation;
  //   op0 = operation[0]; op1 = operation[1]; op2 = operation[2];
  //   ors[11:0] = {or11, or10, or9, or8, or7, or6, or5, or4, or3, or2, or1, or0}; ovf = overflow;
  //   subs[11:0] = {sub11, sub10, sub9, sub8, sub7, sub6, sub5, sub4, sub3, sub2, sub1, sub0}; z = zero
endmodule
