// Logisim project 3.circ as structural Verilog: 1 circuit, main circuit paritygen
module paritygen (
  input  inputw,
  input  sysclock,
  output outputq
);

  wire and_1_out, and_2_out, and_3_out, and_4_out, and_5_out, and_6_out, and_7_out, and_8_out, and_9_out,
       not_5_out, or_1_out, or_2_out, or_3_out, Q1, Q2, Q3, Qn1, Qn2, Qn3, wn;

  not not_1 (wn, inputw);
  and and_1 (and_1_out, Q3, Qn1, inputw);
  and and_2 (and_2_out, Q2, Qn3, wn);
  and and_3 (and_3_out, Q1, Qn3, wn);
  and and_4 (and_4_out, inputw, Qn1, Qn3);
  and and_5 (and_5_out, Q3, Q1, inputw);
  and and_6 (and_6_out, Q3, Qn2, Qn1, wn);
  and and_7 (and_7_out, Q2, inputw);
  and and_8 (and_8_out, Qn2, wn);
  not not_2 (Qn1, Q1);
  not not_3 (Qn2, Q2);
  not not_4 (Qn3, Q3);
  or or_1 (or_1_out, and_1_out, and_2_out, and_3_out);
  or or_2 (or_2_out, and_4_out, and_5_out, and_6_out);
  or or_3 (or_3_out, and_7_out, and_8_out);
  D_Flip_Flop d_ff_1 (.D(or_1_out), .clk(sysclock), .Q(Q1));  // open: Qn, preset, reset
  D_Flip_Flop d_ff_2 (.D(or_2_out), .clk(sysclock), .Q(Q2));  // open: Qn, preset, reset
  D_Flip_Flop d_ff_3 (.D(or_3_out), .clk(sysclock), .Q(Q3));  // open: Qn, preset, reset
  not not_5 (not_5_out, Q3);
  and and_9 (and_9_out, Q2, not_5_out);
  or or_4 (outputq, Q1, and_9_out);

  // Other names for the same wires on the sheet: q = outputq; sc = sysclock; w = inputw
endmodule
