// Logisim project 4.circ as structural Verilog: 1 circuit, main circuit sequencecheck
module sequencecheck (
  input  inputx,
  input  sysclock,
  output outputr
);

  wire and_1_out, and_2_out, and_3_out, and_4_out, and_5_out, and_6_out, and_7_out, and_8_out, and_9_out,
       and_10_out, and_11_out, and_12_out, and_13_out, and_14_out, not_5_out, not_6_out, or_1_out, or_2_out,
       or_3_out, Q0, Q1, Q2, Qn0, Qn1, Qn2, xn;

  and and_1 (and_1_out, Qn2, Q1);
  and and_2 (and_2_out, Q1, Qn0, xn);
  and and_3 (and_3_out, Q2, Qn1, inputx);
  and and_4 (and_4_out, Q2, Qn1, Q0);
  and and_5 (and_5_out, Qn2, Qn1, Qn0);
  and and_6 (and_6_out, Qn1, Qn0, inputx);
  and and_7 (and_7_out, Q2, Qn1, Q0);
  and and_8 (and_8_out, Qn2, Q1, Q0, xn);
  and and_9 (and_9_out, Q2, Q1, Qn0, xn);
  and and_10 (and_10_out, Q2, Qn1);
  and and_11 (and_11_out, Q2, Qn0);
  and and_12 (and_12_out, Qn1, Qn0, inputx);
  and and_13 (and_13_out, Q1, Qn0, xn);
  and and_14 (and_14_out, Qn2, Q1, Q0, inputx);
  or or_1 (or_1_out, and_1_out, and_2_out, and_3_out, and_4_out);
  or or_2 (or_2_out, and_5_out, and_6_out, and_7_out, and_8_out, and_9_out);
  or or_3 (or_3_out, and_10_out, and_11_out, and_12_out, and_13_out, and_14_out);
  D_Flip_Flop d_ff_1 (.D(or_1_out), .clk(sysclock), .Q(Q2));  // open: Qn, preset, reset
  D_Flip_Flop d_ff_2 (.D(or_2_out), .clk(sysclock), .Q(Q1));  // open: Qn, preset, reset
  D_Flip_Flop d_ff_3 (.D(or_3_out), .clk(sysclock), .Q(Q0));  // open: Qn, preset, reset
  not not_1 (xn, inputx);
  not not_2 (Qn0, Q0);
  not not_3 (Qn1, Q1);
  not not_4 (Qn2, Q2);
  not not_5 (not_5_out, Q2);
  not not_6 (not_6_out, Q1);
  and and_15 (outputr, not_5_out, not_6_out, Q0, xn);

  // Other names for the same wires on the sheet: r = outputr; sc = sysclock; x = inputx
endmodule
