// Logisim project 1.circ as structural Verilog: 4 circuits, main circuit alu8
module alu8 (
  input  [11:0] a,
  input  [11:0] b,
  input  [3:0] op,
  input  sysclock,
  output [11:0] alur
);

  wire addsub_1_carry, addsub_1_overflow, and_5_out, and_6_out, and_7_out, carry, mask, not_2_out, not_3_out,
       not_4_out, not_5_out, not_6_out, not_7_out, or_2_out, overflow, zero;
  wire [0:0] comparator_1_eq;
  wire [11:0] addsub_1_answer, and_1_out, not_1_out, or_1_out, shifter_1_out, shifter_2_out, sw, xor_1_out;

  assign not_1_out = ~a;  // NOT_Gate not_1, 12 bits wide
  Comparator #(.width(12)) comparator_1 (.a(a), .b(b), .eq(comparator_1_eq[0]));  // open: gt, lt
  Shifter #(.width(12)) shifter_1 (.in(a), .\dist (4'b0001), .out(shifter_1_out));
  Shifter #(.width(12), .shift("lr")) shifter_2 (.in(a), .\dist (4'b0001), .out(shifter_2_out));
  assign and_1_out = a & b;  // AND_Gate and_1, 12 bits wide
  assign xor_1_out = a ^ b;  // XOR_Gate xor_1, 12 bits wide
  assign or_1_out = a | b;  // OR_Gate or_1, 12 bits wide
  addsub addsub_1 (
    .inputa(a), .inputb(b), .mode(op[0]), .answer(addsub_1_answer), .carry(addsub_1_carry),
    .overflow(addsub_1_overflow));
  not not_2 (not_2_out, op[3]);
  not not_3 (not_3_out, op[1]);
  and and_2 (mask, not_2_out, op[2], not_3_out);
  Register #(.width(12)) register_1 (
    .D({{9{1'b0}}, overflow, carry, zero}), .en(or_2_out), .clk(sysclock), .Q(sw));  // open: clr
  Multiplexer #(.select(4), .width(12), .enable("false")) multiplexer_1 (
    .in0(not_1_out), .in1(and_1_out), .in2(xor_1_out), .in3(or_1_out), .in4(addsub_1_answer),
    .in5(addsub_1_answer), .in6(a), .in7(sw), .in10({{11{1'b0}}, comparator_1_eq[0]}), .in12(shifter_1_out),
    .in13(shifter_2_out), .out(alur), .sel(op));  // open: in8, in9, in11, in14, in15
  nor nor_1 (zero, alur[11], alur[10], alur[9], alur[8], alur[7], alur[6], alur[5], alur[4], alur[3], alur[2], alur[1], alur[0]);
  and and_3 (overflow, addsub_1_overflow, mask);
  and and_4 (carry, mask, addsub_1_carry);
  not not_4 (not_4_out, op[0]);
  not not_5 (not_5_out, op[1]);
  not not_6 (not_6_out, op[2]);
  not not_7 (not_7_out, op[3]);
  and and_5 (and_5_out, not_7_out, not_6_out);
  or or_2 (or_2_out, and_5_out, and_7_out, and_6_out);
  and and_6 (and_6_out, not_6_out, op[1], not_4_out);
  and and_7 (and_7_out, op[2], not_5_out);

  // Other names for the same wires on the sheet: ALUoutput[11:0] = alur; o1 = op[1]; o2 = op[2]; o3 = op[3]
endmodule

module cla6 (
  input  [5:0] inputa,
  input  [5:0] inputb,
  input  carryin,
  output [5:0] carryout,
  output [5:0] generator,
  output [5:0] propagator,
  output [5:0] sum
);

  wire and_7_out, and_8_out, and_9_out, and_10_out, and_11_out, and_12_out, and_13_out, and_14_out,
       and_15_out, and_16_out, and_17_out, and_18_out, and_19_out, and_20_out, and_21_out, and_22_out,
       and_23_out, and_24_out, and_25_out, and_26_out, and_27_out;

  and and_1 (generator[0], inputa[0], inputb[0]);
  xor xor_1 (propagator[0], inputa[0], inputb[0]);
  and and_2 (generator[1], inputa[1], inputb[1]);
  xor xor_2 (propagator[1], inputa[1], inputb[1]);
  and and_3 (generator[2], inputa[2], inputb[2]);
  xor xor_3 (propagator[2], inputa[2], inputb[2]);
  and and_4 (generator[3], inputa[3], inputb[3]);
  xor xor_4 (propagator[3], inputa[3], inputb[3]);
  and and_5 (generator[4], inputa[4], inputb[4]);
  xor xor_5 (propagator[4], inputa[4], inputb[4]);
  and and_6 (generator[5], inputa[5], inputb[5]);
  xor xor_6 (propagator[5], inputa[5], inputb[5]);
  and and_7 (and_7_out, carryin, propagator[0]);
  and and_8 (and_8_out, propagator[1], generator[0]);
  and and_9 (and_9_out, propagator[0], propagator[1], carryin);
  and and_10 (and_10_out, propagator[2], generator[1]);
  and and_11 (and_11_out, propagator[2], propagator[1], generator[0]);
  and and_12 (and_12_out, propagator[2], propagator[1], propagator[0], carryin);
  or or_1 (carryout[0], and_7_out, generator[0]);
  or or_2 (carryout[1], and_8_out, generator[1], and_9_out);
  or or_3 (carryout[2], and_10_out, and_11_out, generator[2], and_12_out);
  and and_13 (and_13_out, propagator[5], generator[4]);
  and and_14 (and_14_out, propagator[5], propagator[4], generator[3]);
  and and_15 (and_15_out, propagator[5], propagator[4], propagator[3], generator[2]);
  and and_16 (and_16_out, propagator[5], propagator[4], propagator[3], propagator[2], generator[1]);
  and and_17 (and_17_out, propagator[5], propagator[4], propagator[3], propagator[2], propagator[1], generator[0]);
  and and_18 (and_18_out, propagator[5], propagator[4], propagator[3], propagator[2], propagator[1], propagator[0], carryin);
  or or_4 (carryout[5], generator[5], and_13_out, and_14_out, and_15_out, and_16_out, and_17_out, and_18_out);
  and and_19 (and_19_out, propagator[3], generator[2]);
  and and_20 (and_20_out, propagator[3], propagator[2], generator[1]);
  and and_21 (and_21_out, propagator[3], propagator[2], propagator[1], generator[0]);
  and and_22 (and_22_out, propagator[3], propagator[2], propagator[1], propagator[0], carryin);
  or or_5 (carryout[3], generator[3], and_19_out, and_20_out, and_21_out, and_22_out);
  and and_23 (and_23_out, propagator[4], generator[3]);
  and and_24 (and_24_out, propagator[4], propagator[3], generator[2]);
  and and_25 (and_25_out, propagator[4], propagator[3], propagator[2], generator[1]);
  and and_26 (and_26_out, propagator[4], propagator[3], propagator[2], propagator[1], generator[0]);
  and and_27 (and_27_out, propagator[4], propagator[3], propagator[2], propagator[1], propagator[0], carryin);
  or or_6 (carryout[4], generator[4], and_23_out, and_24_out, and_25_out, and_26_out, and_27_out);
  xor xor_7 (sum[0], carryin, propagator[0]);
  xor xor_8 (sum[1], carryout[0], propagator[1]);
  xor xor_9 (sum[2], carryout[1], propagator[2]);
  xor xor_10 (sum[3], carryout[2], propagator[3]);
  xor xor_11 (sum[4], carryout[3], propagator[4]);
  xor xor_12 (sum[5], carryout[4], propagator[5]);

  // Other names for the same wires on the sheet: co0 = carryout[0]; co1 = carryout[1]; co2 = carryout[2];
  //   co3 = carryout[3]; co4 = carryout[4]; co5 = carryout[5]; g0 = generator[0]; g1 = generator[1];
  //   g2 = generator[2]; g3 = generator[3]; g4 = generator[4]; g5 = generator[5]; ia0 = inputa[0]; ia1 = inputa[1];
  //   ia2 = inputa[2]; ia3 = inputa[3]; ia4 = inputa[4]; ia5 = inputa[5]; ib0 = inputb[0]; ib1 = inputb[1];
  //   ib2 = inputb[2]; ib3 = inputb[3]; ib4 = inputb[4]; ib5 = inputb[5]; p0 = propagator[0]; p1 = propagator[1];
  //   p2 = propagator[2]; p3 = propagator[3]; p4 = propagator[4]; p5 = propagator[5]; s0 = sum[0]; s1 = sum[1];
  //   s2 = sum[2]; s3 = sum[3]; s4 = sum[4]; s5 = sum[5]
endmodule

module cla12 (
  input  [11:0] inputa,
  input  [11:0] inputb,
  input  carryin,
  output [11:0] answer,
  output carryout,
  output overflowflag
);

  wire secondcarryin;
  wire [4:0] cla6_1_carryout, finalcarry;

  cla6 cla6_1 (
    .inputa(inputa[5:0]), .inputb(inputb[5:0]), .carryin(carryin),
    .carryout({secondcarryin, cla6_1_carryout}), .sum(answer[5:0]));  // open: generator, propagator
  cla6 cla6_2 (
    .inputa(inputa[11:6]), .inputb(inputb[11:6]), .carryin(secondcarryin), .carryout({carryout, finalcarry}),
    .sum(answer[11:6]));  // open: generator, propagator
  xor xor_1 (overflowflag, finalcarry[4], carryout);

  // Other names for the same wires on the sheet: secondtolast = finalcarry[4]; finalcarry[5] = carryout;
  //   ia0[5:0] = inputa[5:0]; ia1[5:0] = inputa[11:6]; ib0[5:0] = inputb[5:0]; ib1[5:0] = inputb[11:6]; m = carryin
endmodule

module addsub (
  input  [11:0] inputa,
  input  [11:0] inputb,
  input  mode,
  output [11:0] answer,
  output carry,
  output overflow
);

  wire [11:0] xor_1_out;

  assign xor_1_out = inputb ^ {12{mode}};  // XOR_Gate xor_1, 12 bits wide
  cla12 cla12_1 (
    .inputa(inputa), .inputb(xor_1_out), .carryin(mode), .answer(answer), .carryout(carry),
    .overflowflag(overflow));
endmodule
