// Logisim project 2.circ as structural Verilog: 1 circuit, main circuit instructions
module instructions (
  input  resetall,
  input  sysclock,
  input  jmp,
  input  [11:0] a,
  output [11:0] pc,
  output [3:0] op,
  output [2:0] rd,
  output [2:0] rs1,
  output [2:0] rs2,
  output [11:0] imm
);

  wire and_1_out, and_2_out, and_3_out, and_4_out, and_5_out, and_6_out, and_7_out, and_8_out, and_9_out,
       and_10_out, and_11_out, and_12_out, and_13_out, and_14_out, and_15_out, and_16_out, and_17_out,
       and_18_out, and_19_out, and_20_out, and_21_out, and_22_out, and_23_out, and_24_out, and_25_out,
       and_26_out, and_27_out, and_28_out, and_29_out, and_30_out, and_31_out, and_32_out, and_33_out,
       and_34_out, and_35_out, and_36_out, not_1_out, not_2_out, not_3_out, not_4_out, not_5_out, not_6_out,
       not_7_out, not_8_out, not_9_out, not_10_out, not_11_out, not_12_out, not_13_out, or_1_out, or_2_out,
       or_3_out, or_4_out, or_5_out, or_6_out, or_7_out, or_8_out, or_9_out, or_10_out, or_11_out, or_12_out,
       or_13_out, or_14_out, or_15_out, or_16_out, or_17_out, or_18_out, or_19_out, or_20_out, or_21_out,
       or_22_out, or_23_out, or_24_out;

  and and_1 (and_1_out, a[0], jmp);
  not not_1 (not_1_out, a[0]);
  and and_2 (and_2_out, not_1_out, jmp);
  not not_2 (not_2_out, jmp);
  and and_3 (and_3_out, not_2_out, 1'b1);
  and and_4 (and_4_out, a[1], jmp);
  not not_3 (not_3_out, a[1]);
  and and_5 (and_5_out, not_3_out, jmp);
  and and_6 (and_6_out, pc[0], and_3_out);
  and and_7 (and_7_out, a[2], jmp);
  not not_4 (not_4_out, a[2]);
  and and_8 (and_8_out, not_4_out, jmp);
  and and_9 (and_9_out, pc[1], and_6_out);
  and and_10 (and_10_out, a[3], jmp);
  not not_5 (not_5_out, a[3]);
  and and_11 (and_11_out, not_5_out, jmp);
  and and_12 (and_12_out, pc[2], and_9_out);
  and and_13 (and_13_out, a[4], jmp);
  not not_6 (not_6_out, a[4]);
  and and_14 (and_14_out, not_6_out, jmp);
  and and_15 (and_15_out, pc[3], and_12_out);
  and and_16 (and_16_out, a[5], jmp);
  not not_7 (not_7_out, a[5]);
  and and_17 (and_17_out, not_7_out, jmp);
  and and_18 (and_18_out, pc[4], and_15_out);
  and and_19 (and_19_out, a[6], jmp);
  not not_8 (not_8_out, a[6]);
  and and_20 (and_20_out, not_8_out, jmp);
  and and_21 (and_21_out, pc[5], and_18_out);
  and and_22 (and_22_out, a[7], jmp);
  not not_9 (not_9_out, a[7]);
  and and_23 (and_23_out, not_9_out, jmp);
  and and_24 (and_24_out, pc[6], and_21_out);
  and and_25 (and_25_out, a[8], jmp);
  not not_10 (not_10_out, a[8]);
  and and_26 (and_26_out, not_10_out, jmp);
  and and_27 (and_27_out, pc[7], and_24_out);
  and and_28 (and_28_out, a[9], jmp);
  not not_11 (not_11_out, a[9]);
  and and_29 (and_29_out, not_11_out, jmp);
  and and_30 (and_30_out, pc[8], and_27_out);
  and and_31 (and_31_out, a[10], jmp);
  not not_12 (not_12_out, a[10]);
  and and_32 (and_32_out, not_12_out, jmp);
  and and_33 (and_33_out, pc[9], and_30_out);
  and and_34 (and_34_out, a[11], jmp);
  not not_13 (not_13_out, a[11]);
  and and_35 (and_35_out, not_13_out, jmp);
  and and_36 (and_36_out, pc[10], and_33_out);
  or or_1 (or_1_out, and_1_out, and_3_out);
  or or_2 (or_2_out, and_2_out, and_3_out);
  or or_3 (or_3_out, and_4_out, and_6_out);
  or or_4 (or_4_out, and_5_out, and_6_out);
  or or_5 (or_5_out, and_7_out, and_9_out);
  or or_6 (or_6_out, and_8_out, and_9_out);
  or or_7 (or_7_out, and_10_out, and_12_out);
  or or_8 (or_8_out, and_11_out, and_12_out);
  or or_9 (or_9_out, and_13_out, and_15_out);
  or or_10 (or_10_out, and_14_out, and_15_out);
  or or_11 (or_11_out, and_16_out, and_18_out);
  or or_12 (or_12_out, and_17_out, and_18_out);
  or or_13 (or_13_out, and_19_out, and_21_out);
  or or_14 (or_14_out, and_20_out, and_21_out);
  or or_15 (or_15_out, and_22_out, and_24_out);
  or or_16 (or_16_out, and_23_out, and_24_out);
  or or_17 (or_17_out, and_25_out, and_27_out);
  or or_18 (or_18_out, and_26_out, and_27_out);
  or or_19 (or_19_out, and_28_out, and_30_out);
  or or_20 (or_20_out, and_29_out, and_30_out);
  or or_21 (or_21_out, and_31_out, and_33_out);
  or or_22 (or_22_out, and_32_out, and_33_out);
  or or_23 (or_23_out, and_34_out, and_36_out);
  or or_24 (or_24_out, and_35_out, and_36_out);
  J_K_Flip_Flop j_k_ff_1 (.J(or_1_out), .K(or_2_out), .clk(sysclock), .Q(pc[0]), .reset(resetall));  // open: Qn, preset
  J_K_Flip_Flop j_k_ff_2 (.J(or_3_out), .K(or_4_out), .clk(sysclock), .Q(pc[1]), .reset(resetall));  // open: Qn, preset
  J_K_Flip_Flop j_k_ff_3 (.J(or_5_out), .K(or_6_out), .clk(sysclock), .Q(pc[2]), .reset(resetall));  // open: Qn, preset
  J_K_Flip_Flop j_k_ff_4 (.J(or_7_out), .K(or_8_out), .clk(sysclock), .Q(pc[3]), .reset(resetall));  // open: Qn, preset
  J_K_Flip_Flop j_k_ff_5 (
    .J(or_9_out), .K(or_10_out), .clk(sysclock), .Q(pc[4]), .reset(resetall));  // open: Qn, preset
  J_K_Flip_Flop j_k_ff_6 (
    .J(or_11_out), .K(or_12_out), .clk(sysclock), .Q(pc[5]), .reset(resetall));  // open: Qn, preset
  J_K_Flip_Flop j_k_ff_7 (
    .J(or_13_out), .K(or_14_out), .clk(sysclock), .Q(pc[6]), .reset(resetall));  // open: Qn, preset
  J_K_Flip_Flop j_k_ff_8 (
    .J(or_15_out), .K(or_16_out), .clk(sysclock), .Q(pc[7]), .reset(resetall));  // open: Qn, preset
  J_K_Flip_Flop j_k_ff_9 (
    .J(or_17_out), .K(or_18_out), .clk(sysclock), .Q(pc[8]), .reset(resetall));  // open: Qn, preset
  J_K_Flip_Flop j_k_ff_10 (
    .J(or_19_out), .K(or_20_out), .clk(sysclock), .Q(pc[9]), .reset(resetall));  // open: Qn, preset
  J_K_Flip_Flop j_k_ff_11 (
    .J(or_21_out), .K(or_22_out), .clk(sysclock), .Q(pc[10]), .reset(resetall));  // open: Qn, preset
  J_K_Flip_Flop j_k_ff_12 (
    .J(or_23_out), .K(or_24_out), .clk(sysclock), .Q(pc[11]), .reset(resetall));  // open: Qn, preset
  RAM #(.addrWidth(12), .dataWidth(25)) ram_1 (
    .addr(pc), .we(1'b0), .oe(1'b1), .clk(sysclock), .data({op, rd, rs1, rs2, imm}));

  // Other names for the same wires on the sheet: p0 = pc[0]; p1 = pc[1]; p2 = pc[2]; p3 = pc[3]; p4 = pc[4];
  //   p5 = pc[5]; p6 = pc[6]; p7 = pc[7]; p8 = pc[8]; p9 = pc[9]; p10 = pc[10]; p11 = pc[11]; rst = resetall;
  //   sc = sysclock
endmodule
