// Logisim project 4.circ as structural Verilog: 7 circuits, main circuit cpu
module cpu (
  input  resetall,
  input  sysclock,
  output [11:0] pc,
  output [11:0] x0,
  output [11:0] x1,
  output [11:0] x2,
  output [11:0] x3,
  output [11:0] x4,
  output [11:0] x5,
  output [11:0] x6,
  output [11:0] x7
);

  wire and_1_out, and_2_out, and_4_out, and_5_out, HCF, HLT, jmp, newsc, not_1_out, not_2_out, not_3_out,
       not_4_out, o0, o1, o2, o3, wen;
  wire [2:0] rd, rs1, rs2;
  wire [11:0] a, alu, b, imm;

  Multiplexer #(.select(3), .width(12), .enable("false")) multiplexer_1 (
    .in0(x0), .in1(x1), .in2(x2), .in3(x3), .in4(x4), .in5(x5), .in6(x6), .in7(x7), .out(a), .sel(rs1));
  Multiplexer #(.select(3), .width(12), .enable("false")) multiplexer_2 (
    .in0(x0), .in1(x1), .in2(x2), .in3(x3), .in4(x4), .in5(x5), .in6(x6), .in7(x7), .out(b), .sel(rs2));
  Multiplexer #(.enable("false")) multiplexer_3 (.in0(sysclock), .in1(1'b0), .out(newsc), .sel(HLT));
  instructions instructions_1 (
    .resetall(resetall), .sysclock(sysclock), .jmp(jmp), .a(a), .pc(pc), .op({o3, o2, o1, o0}), .rd(rd),
    .rs1(rs1), .rs2(rs2), .imm(imm));
  not not_1 (not_1_out, o0);
  not not_2 (not_2_out, o1);
  not not_3 (not_3_out, o2);
  not not_4 (not_4_out, o3);
  and and_1 (and_1_out, o1, o2, o3);
  and and_2 (and_2_out, o3, ~o2, o1, o0);  // AND_Gate
  and and_3 (HCF, o0, o1, o2, o3);
  and and_4 (and_4_out, not_1_out, o1, o2, o3);
  and and_5 (and_5_out, not_1_out, not_3_out);
  and and_6 (jmp, o0, o1, not_3_out, o3);
  alu8 alu8_1 (.a(a), .b(b), .op({o3, o2, o1, o0}), .sysclock(newsc), .alur(alu));
  regfile regfile_1 (
    .rd(rd), .alur(alu), .pc(pc), .imm(imm), .op({o3, o2, o1, o0}), .wen(wen), .resetall(resetall),
    .sysclock(newsc), .x0(x0), .x1(x1), .x2(x2), .x3(x3), .x4(x4), .x5(x5), .x6(x6), .x7(x7));
  and and_7 (wen, ~and_1_out, ~and_2_out);  // AND_Gate
  D_Flip_Flop d_ff_1 (.D(and_4_out), .clk(and_4_out), .Q(HLT), .reset(resetall));  // open: Qn, preset
  or or_1 (wen, not_4_out, not_2_out, and_5_out);

  // Other names for the same wires on the sheet: op[3:0] = {o3, o2, o1, o0}; rst = resetall; sc = sysclock
endmodule

module instructions (
  input  resetall,
  input  sysclock,
  input  jmp,
  input  [11:0] a,
  output [11:0] pc,
  output [3:0] op,
  output [2:0] rd,
  output [2:0] rs1,
  output [2:0] rs2,
  output [11:0] imm
);

  wire and_1_out, and_2_out, and_3_out, and_4_out, and_5_out, and_6_out, and_7_out, and_8_out, and_9_out,
       and_10_out, and_11_out, and_12_out, and_13_out, and_14_out, and_15_out, and_16_out, and_17_out,
       and_18_out, and_19_out, and_20_out, and_21_out, and_22_out, and_23_out, and_24_out, and_25_out,
       and_26_out, and_27_out, and_28_out, and_29_out, and_30_out, and_31_out, and_32_out, and_33_out,
       and_34_out, and_35_out, and_36_out, not_1_out, not_2_out, not_3_out, not_4_out, not_5_out, not_6_out,
       not_7_out, not_8_out, not_9_out, not_10_out, not_11_out, not_12_out, not_13_out, or_1_out, or_2_out,
       or_3_out, or_4_out, or_5_out, or_6_out, or_7_out, or_8_out, or_9_out, or_10_out, or_11_out, or_12_out,
       or_13_out, or_14_out, or_15_out, or_16_out, or_17_out, or_18_out, or_19_out, or_20_out, or_21_out,
       or_22_out, or_23_out, or_24_out;

  and and_1 (and_1_out, a[0], jmp);
  not not_1 (not_1_out, a[0]);
  and and_2 (and_2_out, not_1_out, jmp);
  not not_2 (not_2_out, jmp);
  and and_3 (and_3_out, not_2_out, 1'b1);
  and and_4 (and_4_out, a[1], jmp);
  not not_3 (not_3_out, a[1]);
  and and_5 (and_5_out, not_3_out, jmp);
  and and_6 (and_6_out, pc[0], and_3_out);
  and and_7 (and_7_out, a[2], jmp);
  not not_4 (not_4_out, a[2]);
  and and_8 (and_8_out, not_4_out, jmp);
  and and_9 (and_9_out, pc[1], and_6_out);
  and and_10 (and_10_out, a[3], jmp);
  not not_5 (not_5_out, a[3]);
  and and_11 (and_11_out, not_5_out, jmp);
  and and_12 (and_12_out, pc[2], and_9_out);
  and and_13 (and_13_out, a[4], jmp);
  not not_6 (not_6_out, a[4]);
  and and_14 (and_14_out, not_6_out, jmp);
  and and_15 (and_15_out, pc[3], and_12_out);
  and and_16 (and_16_out, a[5], jmp);
  not not_7 (not_7_out, a[5]);
  and and_17 (and_17_out, not_7_out, jmp);
  and and_18 (and_18_out, pc[4], and_15_out);
  and and_19 (and_19_out, a[6], jmp);
  not not_8 (not_8_out, a[6]);
  and and_20 (and_20_out, not_8_out, jmp);
  and and_21 (and_21_out, pc[5], and_18_out);
  and and_22 (and_22_out, a[7], jmp);
  not not_9 (not_9_out, a[7]);
  and and_23 (and_23_out, not_9_out, jmp);
  and and_24 (and_24_out, pc[6], and_21_out);
  and and_25 (and_25_out, a[8], jmp);
  not not_10 (not_10_out, a[8]);
  and and_26 (and_26_out, not_10_out, jmp);
  and and_27 (and_27_out, pc[7], and_24_out);
  and and_28 (and_28_out, a[9], jmp);
  not not_11 (not_11_out, a[9]);
  and and_29 (and_29_out, not_11_out, jmp);
  and and_30 (and_30_out, pc[8], and_27_out);
  and and_31 (and_31_out, a[10], jmp);
  not not_12 (not_12_out, a[10]);
  and and_32 (and_32_out, not_12_out, jmp);
  and and_33 (and_33_out, pc[9], and_30_out);
  and and_34 (and_34_out, a[11], jmp);
  not not_13 (not_13_out, a[11]);
  and and_35 (and_35_out, not_13_out, jmp);
  and and_36 (and_36_out, pc[10], and_33_out);
  or or_1 (or_1_out, and_1_out, and_3_out);
  or or_2 (or_2_out, and_2_out, and_3_out);
  or or_3 (or_3_out, and_4_out, and_6_out);
  or or_4 (or_4_out, and_5_out, and_6_out);
  or or_5 (or_5_out, and_7_out, and_9_out);
  or or_6 (or_6_out, and_8_out, and_9_out);
  or or_7 (or_7_out, and_10_out, and_12_out);
  or or_8 (or_8_out, and_11_out, and_12_out);
  or or_9 (or_9_out, and_13_out, and_15_out);
  or or_10 (or_10_out, and_14_out, and_15_out);
  or or_11 (or_11_out, and_16_out, and_18_out);
  or or_12 (or_12_out, and_17_out, and_18_out);
  or or_13 (or_13_out, and_19_out, and_21_out);
  or or_14 (or_14_out, and_20_out, and_21_out);
  or or_15 (or_15_out, and_22_out, and_24_out);
  or or_16 (or_16_out, and_23_out, and_24_out);
  or or_17 (or_17_out, and_25_out, and_27_out);
  or or_18 (or_18_out, and_26_out, and_27_out);
  or or_19 (or_19_out, and_28_out, and_30_out);
  or or_20 (or_20_out, and_29_out, and_30_out);
  or or_21 (or_21_out, and_31_out, and_33_out);
  or or_22 (or_22_out, and_32_out, and_33_out);
  or or_23 (or_23_out, and_34_out, and_36_out);
  or or_24 (or_24_out, and_35_out, and_36_out);
  J_K_Flip_Flop j_k_ff_1 (.J(or_1_out), .K(or_2_out), .clk(sysclock), .Q(pc[0]), .reset(resetall));  // open: Qn, preset
  J_K_Flip_Flop j_k_ff_2 (.J(or_3_out), .K(or_4_out), .clk(sysclock), .Q(pc[1]), .reset(resetall));  // open: Qn, preset
  J_K_Flip_Flop j_k_ff_3 (.J(or_5_out), .K(or_6_out), .clk(sysclock), .Q(pc[2]), .reset(resetall));  // open: Qn, preset
  J_K_Flip_Flop j_k_ff_4 (.J(or_7_out), .K(or_8_out), .clk(sysclock), .Q(pc[3]), .reset(resetall));  // open: Qn, preset
  J_K_Flip_Flop j_k_ff_5 (
    .J(or_9_out), .K(or_10_out), .clk(sysclock), .Q(pc[4]), .reset(resetall));  // open: Qn, preset
  J_K_Flip_Flop j_k_ff_6 (
    .J(or_11_out), .K(or_12_out), .clk(sysclock), .Q(pc[5]), .reset(resetall));  // open: Qn, preset
  J_K_Flip_Flop j_k_ff_7 (
    .J(or_13_out), .K(or_14_out), .clk(sysclock), .Q(pc[6]), .reset(resetall));  // open: Qn, preset
  J_K_Flip_Flop j_k_ff_8 (
    .J(or_15_out), .K(or_16_out), .clk(sysclock), .Q(pc[7]), .reset(resetall));  // open: Qn, preset
  J_K_Flip_Flop j_k_ff_9 (
    .J(or_17_out), .K(or_18_out), .clk(sysclock), .Q(pc[8]), .reset(resetall));  // open: Qn, preset
  J_K_Flip_Flop j_k_ff_10 (
    .J(or_19_out), .K(or_20_out), .clk(sysclock), .Q(pc[9]), .reset(resetall));  // open: Qn, preset
  J_K_Flip_Flop j_k_ff_11 (
    .J(or_21_out), .K(or_22_out), .clk(sysclock), .Q(pc[10]), .reset(resetall));  // open: Qn, preset
  J_K_Flip_Flop j_k_ff_12 (
    .J(or_23_out), .K(or_24_out), .clk(sysclock), .Q(pc[11]), .reset(resetall));  // open: Qn, preset
  RAM #(.addrWidth(12), .dataWidth(25)) ram_1 (
    .addr(pc), .we(1'b0), .oe(1'b1), .clk(sysclock), .data({op, rd, rs1, rs2, imm}));

  // Other names for the same wires on the sheet: p0 = pc[0]; p1 = pc[1]; p2 = pc[2]; p3 = pc[3]; p4 = pc[4];
  //   p5 = pc[5]; p6 = pc[6]; p7 = pc[7]; p8 = pc[8]; p9 = pc[9]; p10 = pc[10]; p11 = pc[11]; rst = resetall;
  //   sc = sysclock
endmodule

module regfile (
  input  [2:0] rd,
  input  [11:0] alur,
  input  [11:0] pc,
  input  [11:0] imm,
  input  [3:0] op,
  input  wen,
  input  resetall,
  input  sysclock,
  output [11:0] x0,
  output [11:0] x1,
  output [11:0] x2,
  output [11:0] x3,
  output [11:0] x4,
  output [11:0] x5,
  output [11:0] x6,
  output [11:0] x7
);

  wire decoder_1_out0, decoder_1_out1, decoder_1_out2, decoder_1_out3, decoder_1_out4, decoder_1_out5,
       decoder_1_out6, decoder_1_out7;
  wire [11:0] outp;

  Multiplexer #(.select(4), .width(12), .enable("false")) multiplexer_1 (
    .in0(alur), .in1(alur), .in2(alur), .in3(alur), .in4(alur), .in5(alur), .in6(alur), .in7(alur), .in8(pc),
    .in9(imm), .in10(alur), .in11(alur), .in12(alur), .in13(alur), .out(outp), .sel(op));  // open: in14, in15
  Decoder #(.select(3)) decoder_1 (
    .out0(decoder_1_out0), .out1(decoder_1_out1), .out2(decoder_1_out2), .out3(decoder_1_out3),
    .out4(decoder_1_out4), .out5(decoder_1_out5), .out6(decoder_1_out6), .out7(decoder_1_out7), .sel(rd),
    .en(wen));
  Register #(.width(12)) register_1 (.D(outp), .en(decoder_1_out0), .clk(sysclock), .Q(x0), .clr(resetall));
  Register #(.width(12)) register_2 (.D(outp), .en(decoder_1_out1), .clk(sysclock), .Q(x1), .clr(resetall));
  Register #(.width(12)) register_3 (.D(outp), .en(decoder_1_out2), .clk(sysclock), .Q(x2), .clr(resetall));
  Register #(.width(12)) register_4 (.D(outp), .en(decoder_1_out3), .clk(sysclock), .Q(x3), .clr(resetall));
  Register #(.width(12)) register_5 (.D(outp), .en(decoder_1_out4), .clk(sysclock), .Q(x4), .clr(resetall));
  Register #(.width(12)) register_6 (.D(outp), .en(decoder_1_out5), .clk(sysclock), .Q(x5), .clr(resetall));
  Register #(.width(12)) register_7 (.D(outp), .en(decoder_1_out6), .clk(sysclock), .Q(x6), .clr(resetall));
  Register #(.width(12)) register_8 (.D(outp), .en(decoder_1_out7), .clk(sysclock), .Q(x7), .clr(resetall));

  // Other names for the same wires on the sheet: alu[11:0] = alur; rst = resetall; sc = sysclock
endmodule

module cla6 (
  input  [5:0] inputa,
  input  [5:0] inputb,
  input  carryin,
  output [5:0] carryout,
  output [5:0] generator,
  output [5:0] propagator,
  output [5:0] sum
);

  wire and_7_out, and_8_out, and_9_out, and_10_out, and_11_out, and_12_out, and_13_out, and_14_out,
       and_15_out, and_16_out, and_17_out, and_18_out, and_19_out, and_20_out, and_21_out, and_22_out,
       and_23_out, and_24_out, and_25_out, and_26_out, and_27_out;

  and and_1 (generator[0], inputa[0], inputb[0]);
  xor xor_1 (propagator[0], inputa[0], inputb[0]);
  and and_2 (generator[1], inputa[1], inputb[1]);
  xor xor_2 (propagator[1], inputa[1], inputb[1]);
  and and_3 (generator[2], inputa[2], inputb[2]);
  xor xor_3 (propagator[2], inputa[2], inputb[2]);
  and and_4 (generator[3], inputa[3], inputb[3]);
  xor xor_4 (propagator[3], inputa[3], inputb[3]);
  and and_5 (generator[4], inputa[4], inputb[4]);
  xor xor_5 (propagator[4], inputa[4], inputb[4]);
  and and_6 (generator[5], inputa[5], inputb[5]);
  xor xor_6 (propagator[5], inputa[5], inputb[5]);
  and and_7 (and_7_out, carryin, propagator[0]);
  and and_8 (and_8_out, propagator[1], generator[0]);
  and and_9 (and_9_out, propagator[0], propagator[1], carryin);
  and and_10 (and_10_out, propagator[2], generator[1]);
  and and_11 (and_11_out, propagator[2], propagator[1], generator[0]);
  and and_12 (and_12_out, propagator[2], propagator[1], propagator[0], carryin);
  or or_1 (carryout[0], and_7_out, generator[0]);
  or or_2 (carryout[1], and_8_out, generator[1], and_9_out);
  or or_3 (carryout[2], and_10_out, and_11_out, generator[2], and_12_out);
  and and_13 (and_13_out, propagator[5], generator[4]);
  and and_14 (and_14_out, propagator[5], propagator[4], generator[3]);
  and and_15 (and_15_out, propagator[5], propagator[4], propagator[3], generator[2]);
  and and_16 (and_16_out, propagator[5], propagator[4], propagator[3], propagator[2], generator[1]);
  and and_17 (and_17_out, propagator[5], propagator[4], propagator[3], propagator[2], propagator[1], generator[0]);
  and and_18 (and_18_out, propagator[5], propagator[4], propagator[3], propagator[2], propagator[1], propagator[0], carryin);
  or or_4 (carryout[5], generator[5], and_13_out, and_14_out, and_15_out, and_16_out, and_17_out, and_18_out);
  and and_19 (and_19_out, propagator[3], generator[2]);
  and and_20 (and_20_out, propagator[3], propagator[2], generator[1]);
  and and_21 (and_21_out, propagator[3], propagator[2], propagator[1], generator[0]);
  and and_22 (and_22_out, propagator[3], propagator[2], propagator[1], propagator[0], carryin);
  or or_5 (carryout[3], generator[3], and_19_out, and_20_out, and_21_out, and_22_out);
  and and_23 (and_23_out, propagator[4], generator[3]);
  and and_24 (and_24_out, propagator[4], propagator[3], generator[2]);
  and and_25 (and_25_out, propagator[4], propagator[3], propagator[2], generator[1]);
  and and_26 (and_26_out, propagator[4], propagator[3], propagator[2], propagator[1], generator[0]);
  and and_27 (and_27_out, propagator[4], propagator[3], propagator[2], propagator[1], propagator[0], carryin);
  or or_6 (carryout[4], generator[4], and_23_out, and_24_out, and_25_out, and_26_out, and_27_out);
  xor xor_7 (sum[0], carryin, propagator[0]);
  xor xor_8 (sum[1], carryout[0], propagator[1]);
  xor xor_9 (sum[2], carryout[1], propagator[2]);
  xor xor_10 (sum[3], carryout[2], propagator[3]);
  xor xor_11 (sum[4], carryout[3], propagator[4]);
  xor xor_12 (sum[5], carryout[4], propagator[5]);

  // Other names for the same wires on the sheet: co0 = carryout[0]; co1 = carryout[1]; co2 = carryout[2];
  //   co3 = carryout[3]; co4 = carryout[4]; co5 = carryout[5]; g0 = generator[0]; g1 = generator[1];
  //   g2 = generator[2]; g3 = generator[3]; g4 = generator[4]; g5 = generator[5]; ia0 = inputa[0]; ia1 = inputa[1];
  //   ia2 = inputa[2]; ia3 = inputa[3]; ia4 = inputa[4]; ia5 = inputa[5]; ib0 = inputb[0]; ib1 = inputb[1];
  //   ib2 = inputb[2]; ib3 = inputb[3]; ib4 = inputb[4]; ib5 = inputb[5]; p0 = propagator[0]; p1 = propagator[1];
  //   p2 = propagator[2]; p3 = propagator[3]; p4 = propagator[4]; p5 = propagator[5]; s0 = sum[0]; s1 = sum[1];
  //   s2 = sum[2]; s3 = sum[3]; s4 = sum[4]; s5 = sum[5]
endmodule

module cla12 (
  input  [11:0] inputa,
  input  [11:0] inputb,
  input  carryin,
  output [11:0] answer,
  output carryout,
  output overflowflag
);

  wire secondcarryin;
  wire [4:0] cla6_1_carryout, finalcarry;

  cla6 cla6_1 (
    .inputa(inputa[5:0]), .inputb(inputb[5:0]), .carryin(carryin),
    .carryout({secondcarryin, cla6_1_carryout}), .sum(answer[5:0]));  // open: generator, propagator
  cla6 cla6_2 (
    .inputa(inputa[11:6]), .inputb(inputb[11:6]), .carryin(secondcarryin), .carryout({carryout, finalcarry}),
    .sum(answer[11:6]));  // open: generator, propagator
  xor xor_1 (overflowflag, finalcarry[4], carryout);

  // Other names for the same wires on the sheet: secondtolast = finalcarry[4]; finalcarry[5] = carryout;
  //   ia0[5:0] = inputa[5:0]; ia1[5:0] = inputa[11:6]; ib0[5:0] = inputb[5:0]; ib1[5:0] = inputb[11:6]; m = carryin
endmodule

module addsub (
  input  [11:0] inputa,
  input  [11:0] inputb,
  input  mode,
  output [11:0] answer,
  output carry,
  output overflow
);

  wire [11:0] xor_1_out;

  assign xor_1_out = inputb ^ {12{mode}};  // XOR_Gate xor_1, 12 bits wide
  cla12 cla12_1 (
    .inputa(inputa), .inputb(xor_1_out), .carryin(mode), .answer(answer), .carryout(carry),
    .overflowflag(overflow));
endmodule

module alu8 (
  input  [11:0] a,
  input  [11:0] b,
  input  [3:0] op,
  input  sysclock,
  output [11:0] alur
);

  wire addsub_1_carry, addsub_1_overflow, and_5_out, and_6_out, and_7_out, carry, mask, not_2_out, not_3_out,
       not_4_out, not_5_out, not_6_out, not_7_out, or_2_out, overflow, zero;
  wire [0:0] comparator_1_eq;
  wire [11:0] addsub_1_answer, and_1_out, not_1_out, or_1_out, shifter_1_out, shifter_2_out, sw, xor_1_out;

  assign not_1_out = ~a;  // NOT_Gate not_1, 12 bits wide
  Comparator #(.width(12)) comparator_1 (.a(a), .b(b), .eq(comparator_1_eq[0]));  // open: gt, lt
  Shifter #(.width(12)) shifter_1 (.in(a), .\dist (4'b0001), .out(shifter_1_out));
  Shifter #(.width(12), .shift("lr")) shifter_2 (.in(a), .\dist (4'b0001), .out(shifter_2_out));
  assign and_1_out = a & b;  // AND_Gate and_1, 12 bits wide
  assign xor_1_out = a ^ b;  // XOR_Gate xor_1, 12 bits wide
  assign or_1_out = a | b;  // OR_Gate or_1, 12 bits wide
  addsub addsub_1 (
    .inputa(a), .inputb(b), .mode(op[0]), .answer(addsub_1_answer), .carry(addsub_1_carry),
    .overflow(addsub_1_overflow));
  not not_2 (not_2_out, op[3]);
  not not_3 (not_3_out, op[1]);
  and and_2 (mask, not_2_out, op[2], not_3_out);
  Register #(.width(12)) register_1 (
    .D({{9{1'b0}}, overflow, carry, zero}), .en(or_2_out), .clk(sysclock), .Q(sw));  // open: clr
  Multiplexer #(.select(4), .width(12), .enable("false")) multiplexer_1 (
    .in0(not_1_out), .in1(and_1_out), .in2(xor_1_out), .in3(or_1_out), .in4(addsub_1_answer),
    .in5(addsub_1_answer), .in6(a), .in7(sw), .in10({{11{1'b0}}, comparator_1_eq[0]}), .in12(shifter_1_out),
    .in13(shifter_2_out), .out(alur), .sel(op));  // open: in8, in9, in11, in14, in15
  nor nor_1 (zero, alur[11], alur[10], alur[9], alur[8], alur[7], alur[6], alur[5], alur[4], alur[3], alur[2], alur[1], alur[0]);
  and and_3 (overflow, addsub_1_overflow, mask);
  and and_4 (carry, mask, addsub_1_carry);
  not not_4 (not_4_out, op[0]);
  not not_5 (not_5_out, op[1]);
  not not_6 (not_6_out, op[2]);
  not not_7 (not_7_out, op[3]);
  and and_5 (and_5_out, not_7_out, not_6_out);
  or or_2 (or_2_out, and_5_out, and_6_out, and_7_out);
  and and_6 (and_6_out, op[2], not_5_out);
  and and_7 (and_7_out, not_6_out, op[1], not_4_out);

  // Other names for the same wires on the sheet: ALUoutput[11:0] = alur; o1 = op[1]; o2 = op[2]; o3 = op[3]
endmodule
