// Logisim project 3tester.circ as structural Verilog: 1 circuit, main circuit main
module main (
  output halt,
  output [2:0] out_2,
  output [11:0] out_3,
  output [11:0] out_4,
  output [11:0] out_5,
  output [3:0] out_6,
  output wen,
  output out_8,
  output [11:0] out_9,
  output [11:0] out_10,
  output [11:0] out_11,
  output [11:0] out_12,
  output [11:0] out_13,
  output [11:0] out_14,
  output [11:0] out_15,
  output [11:0] out_16
);

  wire and_2_out, and_3_out, clock_1_out;
  wire [5:0] random_1_out;

  Clock clock_1 (.out(clock_1_out));
  Counter #(.width(7), .max('h7f)) counter_1 (
    .clk(clock_1_out), .carry(halt), .Q({out_6, out_2}));  // open: clr, load, up, count, D
  Random #(.width(6), .seed(666)) random_1 (.next(1'b1), .clk(clock_1_out), .out(random_1_out));  // open: clr
  and and_1 (out_8, random_1_out[2], random_1_out[3], random_1_out[4], random_1_out[5]);
  and and_2 (and_2_out, out_6[1], out_6[2], out_6[3]);
  and and_3 (and_3_out, out_6[3], ~out_6[2], out_6[1], out_6[0]);  // AND_Gate
  and and_4 (wen, ~and_2_out, ~and_3_out);  // AND_Gate
  Random #(.width(12), .seed(66)) random_2 (.next(1'b1), .clk(clock_1_out), .out(out_3));  // open: clr
  Random #(.width(12), .seed(670)) random_3 (.next(1'b1), .clk(clock_1_out), .out(out_4));  // open: clr
  Random #(.width(12), .seed(672)) random_4 (.next(1'b1), .clk(clock_1_out), .out(out_5));  // open: clr
  regfile regfile_1 (
    .rd(out_2), .alur(out_3), .pc(out_4), .imm(out_5), .op(out_6), .wen(wen), .resetall(out_8),
    .sysclock(clock_1_out), .x0(out_9), .x1(out_10), .x2(out_11), .x3(out_12), .x4(out_13), .x5(out_14),
    .x6(out_15), .x7(out_16));

  // Other names for the same wires on the sheet: alur[11:0] = out_3; imm[11:0] = out_5; pc[11:0] = out_4; rst = out_8

  // Notes on the sheet:
  //   Place your circuit here ^
endmodule
