// Logisim project 2_soln.circ as structural Verilog: 1 circuit, main circuit minterm
module minterm (
  input  [3:0] fourbitinput,
  output h
);

  wire not_1_out;

  not not_1 (not_1_out, fourbitinput[2]);
  and and_1 (h, fourbitinput[0], fourbitinput[1], not_1_out, fourbitinput[3]);

  // Notes on the sheet:
  //   h = x3 !x2 x1 x0
endmodule
