// Logisim project 3_soln.circ as structural Verilog: 1 circuit, main circuit maxterm
module maxterm (
  input  [3:0] fourbitinput,
  output j
);

  wire not_1_out, not_2_out;

  not not_1 (not_1_out, fourbitinput[0]);
  not not_2 (not_2_out, fourbitinput[3]);
  or or_1 (j, not_1_out, fourbitinput[1], fourbitinput[2], not_2_out);

  // Notes on the sheet:
  //   j = !x3 + x2 + x1 + !x0 
endmodule
