// Logisim project 4_soln.circ as structural Verilog: 1 circuit, main circuit karnaugh
module karnaugh (
  input  [3:0] fourbitinput,
  output k
);

  wire and_1_out, and_2_out, and_3_out, and_4_out, and_5_out, not_1_out, not_2_out, not_3_out, not_4_out;

  not not_1 (not_1_out, fourbitinput[3]);
  not not_2 (not_2_out, fourbitinput[1]);
  not not_3 (not_3_out, fourbitinput[2]);
  not not_4 (not_4_out, fourbitinput[0]);
  and and_1 (and_1_out, not_4_out, not_2_out, not_1_out);
  and and_2 (and_2_out, fourbitinput[0], fourbitinput[1], not_1_out);
  and and_3 (and_3_out, not_4_out, fourbitinput[2], not_1_out);
  and and_4 (and_4_out, fourbitinput[1], not_3_out, fourbitinput[3]);
  and and_5 (and_5_out, fourbitinput[0], not_2_out, fourbitinput[2], fourbitinput[3]);
  or or_1 (k, and_1_out, and_2_out, and_3_out, and_4_out, and_5_out);

  // Notes on the sheet:
  //   k = !x3 !x1 !x0 + !x3 x1 x0 + !x3 x2 !x0 + x3 !x2 x1 + x3 x2 !x1 x0
endmodule
