// Logisim project 5_soln.circ as structural Verilog: 1 circuit, main circuit singledigit
module singledigit (
  input  [3:0] i,
  output a,
  output b,
  output c,
  output d,
  output e,
  output f,
  output g
);

  wire and_1_out, and_2_out, and_3_out, and_4_out, and_5_out, and_6_out, and_7_out, and_8_out, and_9_out,
       and_10_out, and_11_out, and_12_out, and_13_out, and_14_out, and_15_out, and_16_out, w_bar, x_bar,
       y_bar, z_bar;

  _7_Segment_Display u_7_segment_display_1 (.g(g), .f(f), .a(a), .b(b), .e(e), .d(d), .c(c));  // open: dp
  not not_1 (z_bar, i[0]);
  not not_2 (y_bar, i[1]);
  not not_3 (x_bar, i[2]);
  not not_4 (w_bar, i[3]);
  and and_1 (and_1_out, x_bar, z_bar);
  and and_2 (and_2_out, i[2], i[0]);
  and and_3 (and_3_out, y_bar, z_bar);
  and and_4 (and_4_out, i[1], i[0]);
  or or_1 (a, i[3], i[1], and_1_out, and_2_out);
  or or_2 (b, x_bar, and_3_out, and_4_out);
  or or_3 (c, y_bar, i[0], i[2]);
  and and_5 (and_5_out, x_bar, z_bar);
  and and_6 (and_6_out, x_bar, i[1]);
  and and_7 (and_7_out, i[1], z_bar);
  and and_8 (and_8_out, i[2], y_bar, i[0]);
  and and_9 (and_9_out, x_bar, z_bar);
  and and_10 (and_10_out, i[1], z_bar);
  and and_11 (and_11_out, y_bar, z_bar);
  and and_12 (and_12_out, i[2], y_bar);
  and and_13 (and_13_out, i[2], z_bar);
  and and_14 (and_14_out, x_bar, i[1]);
  and and_15 (and_15_out, i[1], z_bar);
  and and_16 (and_16_out, i[2], y_bar);
  or or_4 (d, i[3], and_5_out, and_6_out, and_7_out, and_8_out);
  or or_5 (e, and_9_out, and_10_out);
  or or_6 (f, i[3], and_11_out, and_12_out, and_13_out);
  or or_7 (g, i[3], and_14_out, and_15_out, and_16_out);

  // Other names for the same wires on the sheet: z = i[0]; y = i[1]; x = i[2]; w = i[3]

  // Notes on the sheet:
  //   a = y + w + x'z' + xz
  //   b = x' + y'z' + yz
  //   c = y' + z + x
  //   d = w + x'z' + x'y + yz' + xy'z
  //   e = x'z' + yz'
  //   f = w + y'z' + xy' + xz'
  //   g = w + x'y + yz' + xy'
endmodule
