// Logisim project 6_soln.circ as structural Verilog: 1 circuit, main circuit multiplexor
module multiplexor (
  input  [2:0] inputzero,
  input  [2:0] inputone,
  input  [2:0] inputtwo,
  input  [2:0] inputthree,
  input  [1:0] selector,
  output [2:0] muxoutput
);

  wire and_5_out, and_6_out, and_7_out, and_8_out, and_9_out, and_10_out, and_11_out, and_12_out, and_13_out,
       and_14_out, and_15_out, and_16_out, s0_bar, s1_bar;
  wire [2:0] and_1_out, and_2_out, and_3_out, and_4_out, oc;

  not not_1 (s1_bar, selector[1]);
  not not_2 (s0_bar, selector[0]);
  assign and_1_out = {3{s0_bar}} & {3{s1_bar}} & inputzero;  // AND_Gate and_1, 3 bits wide
  assign and_2_out = {3{selector[0]}} & {3{s1_bar}} & inputone;  // AND_Gate and_2, 3 bits wide
  assign and_3_out = {3{selector[1]}} & {3{s0_bar}} & inputtwo;  // AND_Gate and_3, 3 bits wide
  assign and_4_out = {3{selector[0]}} & {3{selector[1]}} & inputthree;  // AND_Gate and_4, 3 bits wide
  assign muxoutput = and_1_out | and_2_out | and_3_out | and_4_out;  // OR_Gate or_1, 3 bits wide
  and and_5 (and_5_out, s1_bar, s0_bar, inputzero[2]);
  and and_6 (and_6_out, s1_bar, selector[0], inputone[2]);
  and and_7 (and_7_out, selector[1], s0_bar, inputtwo[2]);
  and and_8 (and_8_out, selector[1], selector[0], inputthree[2]);
  or or_2 (oc[2], and_5_out, and_6_out, and_7_out, and_8_out);
  and and_9 (and_9_out, s1_bar, s0_bar, inputzero[1]);
  and and_10 (and_10_out, s1_bar, selector[0], inputone[1]);
  and and_11 (and_11_out, selector[1], s0_bar, inputtwo[1]);
  and and_12 (and_12_out, selector[1], selector[0], inputthree[1]);
  or or_3 (oc[1], and_12_out, and_11_out, and_10_out, and_9_out);
  and and_13 (and_13_out, s1_bar, s0_bar, inputzero[0]);
  and and_14 (and_14_out, s1_bar, selector[0], inputone[0]);
  and and_15 (and_15_out, selector[1], s0_bar, inputtwo[0]);
  and and_16 (and_16_out, selector[1], selector[0], inputthree[0]);
  or or_4 (oc[0], and_16_out, and_15_out, and_14_out, and_13_out);

  // Other names for the same wires on the sheet: s1 = selector[1]; s0 = selector[0]; i0[2:0] = inputzero;
  //   i1[2:0] = inputone; i2[2:0] = inputtwo; i3[2:0] = inputthree; ob[2:0] = muxoutput

  // Notes on the sheet:
  //   connect to "oc" to test the other design
  //   Compact design using Gates with bus inputs
  //   comprehensive design
endmodule
