// Logisim project 1_soln.circ as structural Verilog: 1 circuit, main circuit bitcounting
module bitcounting (
  input  [11:0] twelvebitinput,
  output [3:0] zeroes
);

  wire and_8_out, and_9_out, and_10_out, and_11_out, and_12_out, and_13_out, and_14_out, or_3_out;
  wire [1:0] and_4_out, and_5_out, and_6_out, and_7_out, or_2_out, xor_2_out, xor_3_out;
  wire [3:0] a, and_1_out, and_2_out, and_3_out, b, c, or_1_out, xor_1_out;

  assign xor_1_out = a ^ b ^ c;  // XOR_Gate xor_1, 4 bits wide
  assign and_1_out = a & b;  // AND_Gate and_1, 4 bits wide
  assign and_2_out = b & c;  // AND_Gate and_2, 4 bits wide
  assign and_3_out = c & a;  // AND_Gate and_3, 4 bits wide
  assign or_1_out = and_1_out | and_2_out | and_3_out;  // OR_Gate or_1, 4 bits wide
  assign xor_2_out = xor_1_out[1:0] ^ xor_1_out[3:2];  // XOR_Gate xor_2, 2 bits wide
  assign and_4_out = xor_1_out[1:0] & xor_1_out[3:2];  // AND_Gate and_4, 2 bits wide
  assign xor_3_out = and_4_out ^ or_1_out[1:0] ^ or_1_out[3:2];  // XOR_Gate xor_3, 2 bits wide
  assign and_5_out = and_4_out & or_1_out[1:0];  // AND_Gate and_5, 2 bits wide
  assign and_6_out = or_1_out[1:0] & or_1_out[3:2];  // AND_Gate and_6, 2 bits wide
  assign and_7_out = or_1_out[3:2] & and_4_out;  // AND_Gate and_7, 2 bits wide
  assign or_2_out = and_5_out | and_6_out | and_7_out;  // OR_Gate or_2, 2 bits wide
  not not_1 (a[2], twelvebitinput[10]);
  not not_2 (a[3], twelvebitinput[11]);
  not not_3 (a[0], twelvebitinput[8]);
  not not_4 (a[1], twelvebitinput[9]);
  not not_5 (b[3], twelvebitinput[7]);
  xor xor_4 (zeroes[0], xor_2_out[0], xor_2_out[1]);
  and and_8 (and_8_out, xor_2_out[0], xor_2_out[1]);
  xor xor_5 (zeroes[1], and_8_out, xor_3_out[0], xor_3_out[1]);
  and and_9 (and_9_out, and_8_out, xor_3_out[0]);
  and and_10 (and_10_out, xor_3_out[0], xor_3_out[1]);
  and and_11 (and_11_out, xor_3_out[1], and_8_out);
  xor xor_6 (zeroes[2], or_3_out, or_2_out[0], or_2_out[1]);
  and and_12 (and_12_out, or_3_out, or_2_out[0]);
  and and_13 (and_13_out, or_2_out[0], or_2_out[1]);
  and and_14 (and_14_out, or_2_out[1], or_3_out);
  not not_6 (b[2], twelvebitinput[6]);
  not not_7 (b[1], twelvebitinput[5]);
  or or_3 (or_3_out, and_9_out, and_10_out, and_11_out);
  or or_4 (zeroes[3], and_12_out, and_13_out, and_14_out);
  not not_8 (b[0], twelvebitinput[4]);
  not not_9 (c[3], twelvebitinput[3]);
  not not_10 (c[2], twelvebitinput[2]);
  not not_11 (c[1], twelvebitinput[1]);
  not not_12 (c[0], twelvebitinput[0]);

  // Other names for the same wires on the sheet: p0 = zeroes[0]; p1 = zeroes[1]; p2 = zeroes[2]; p3 = zeroes[3]

  // Notes on the sheet:
  //   4-wide 1-adder
  //   !x0 + !x4 + !x8 
  //   !x1 + !x5 + !x9 
  //   !x2 + !x6 + !x10 
  //   !x3 + !x7 + !x11 
  //   x11 x10 x9 x8 x7 x6 x5 x4 x3 x2 x1 x0
  //   2-wide 2-adder
  //   !x0 + !x4 + !x8 + !x2 + !x6 + !x10
  //   !x1 + !x5 + !x9 + !x3 + !x7 + !x11
  //   3-adder
  //   !x0 + !x4 + !x8 + !x2 + !x6 + !x10 + !x1 + !x5 + !x9 + !x3 + !x7 + !x11
endmodule
