// Logisim project 1_soln2.circ as structural Verilog: 1 circuit, main circuit bitcounting
module bitcounting (
  input  [11:0] twelvebitinput,
  output [3:0] zeroes
);

  wire a, b, c, d, e, f, g, h, i, j, k, l;
  wire [1:0] adder_1_out, adder_2_out, adder_3_out, adder_4_out, adder_5_out, adder_6_out;
  wire [2:2] adder_5_cout, adder_6_cout;

  Adder #(.width(1)) adder_1 (.a(b), .b(c), .out(adder_1_out[0]), .cin(a), .cout(adder_1_out[1]));
  Adder #(.width(1)) adder_2 (.a(e), .b(f), .out(adder_2_out[0]), .cin(d), .cout(adder_2_out[1]));
  Adder #(.width(1)) adder_3 (.a(h), .b(i), .out(adder_3_out[0]), .cin(g), .cout(adder_3_out[1]));
  Adder #(.width(1)) adder_4 (.a(k), .b(l), .out(adder_4_out[0]), .cin(j), .cout(adder_4_out[1]));
  Adder #(.width(2)) adder_5 (
    .a(adder_1_out), .b(adder_2_out), .out(adder_5_out), .cout(adder_5_cout[2]));  // open: cin
  Adder #(.width(2)) adder_6 (
    .a(adder_3_out), .b(adder_4_out), .out(adder_6_out), .cout(adder_6_cout[2]));  // open: cin
  not not_1 (b, twelvebitinput[10]);
  not not_2 (a, twelvebitinput[11]);
  not not_3 (d, twelvebitinput[8]);
  not not_4 (c, twelvebitinput[9]);
  not not_5 (e, twelvebitinput[7]);
  Adder #(.width(3)) adder_7 (
    .a({adder_5_cout[2], adder_5_out}), .b({adder_6_cout[2], adder_6_out}), .out(zeroes[2:0]),
    .cout(zeroes[3]));  // open: cin
  not not_6 (f, twelvebitinput[6]);
  not not_7 (g, twelvebitinput[5]);
  not not_8 (h, twelvebitinput[4]);
  not not_9 (i, twelvebitinput[3]);
  not not_10 (j, twelvebitinput[2]);
  not not_11 (k, twelvebitinput[1]);
  not not_12 (l, twelvebitinput[0]);

  // Other names for the same wires on the sheet: p0 = zeroes[0]; p1 = zeroes[1]; p2 = zeroes[2]; p3 = zeroes[3]

  // Notes on the sheet:
  //   four 1-bit adders
  //   two 2-bit adders
  //   one 3-bit adder
endmodule
