// Logisim project 2_soln.circ as structural Verilog: 1 circuit, main circuit comparison
module comparison (
  input  [1:0] inputa,
  input  [1:0] inputb,
  output areequal,
  output greaterthan,
  output lessthan
);

  wire nand_1_out, nand_2_out, nand_3_out, nand_4_out, nand_5_out, nand_6_out, nand_9_out;

  nand nand_1 (nand_1_out, inputb[1], inputa[1]);
  nand nand_2 (nand_2_out, inputb[0], inputa[0]);
  nand nand_3 (nand_3_out, inputa[1], nand_1_out);
  nand nand_4 (nand_4_out, nand_1_out, inputb[1]);
  nand nand_5 (nand_5_out, nand_2_out, inputb[0], nand_3_out);
  nand nand_6 (nand_6_out, nand_4_out, inputa[0], nand_2_out);
  nand nand_7 (lessthan, nand_5_out, nand_4_out);
  nand nand_8 (greaterthan, nand_3_out, nand_6_out);
  nand nand_9 (nand_9_out, nand_4_out, nand_5_out, nand_6_out, nand_3_out);
  nand nand_10 (areequal, nand_9_out, nand_9_out);

  // Other names for the same wires on the sheet: e = areequal; g = greaterthan; l = lessthan

  // Notes on the sheet:
  //   a1 a0
  //   b1 b0
  //   b1
  //   !(a1 b1)
  //   a1
  //   !(a0 b0)
  //   10 NANDs solution
  //   a0
  //   !(a1 !b1)
  //   !(!a1 b1)
  //   lesser than circuit
  //   l =  !a1 b1 + !(a1 !b1) (!a0 b0) 
  //   g =  a1 !b1 + !(!a1 b1) (a0 !b0)
  //   greater than circuit
  //   e = !g !l
  //   equal to circuit
endmodule
