// Logisim project 2_soln2.circ as structural Verilog: 1 circuit, main circuit comparison
module comparison (
  input  [1:0] inputa,
  input  [1:0] inputb,
  output areequal,
  output greaterthan,
  output lessthan
);

  wire nand_1_out, nand_2_out, nand_3_out, nand_4_out, nand_5_out, nand_6_out, nand_7_out, nand_8_out,
       nand_9_out, nand_10_out, nand_12_out;

  nand nand_1 (nand_1_out, inputb[1], inputb[1]);
  nand nand_2 (nand_2_out, inputb[0], inputb[0]);
  nand nand_3 (nand_3_out, inputa[1], inputa[1]);
  nand nand_4 (nand_4_out, inputa[0], inputa[0]);
  nand nand_5 (nand_5_out, inputa[0], nand_2_out, inputa[1]);
  nand nand_6 (nand_6_out, inputa[0], nand_2_out, nand_1_out);
  nand nand_7 (nand_7_out, inputa[1], nand_1_out);
  nand nand_8 (nand_8_out, inputb[0], nand_4_out, inputb[1]);
  nand nand_9 (nand_9_out, inputb[0], nand_4_out, nand_3_out);
  nand nand_10 (nand_10_out, inputb[1], nand_3_out);
  nand nand_11 (greaterthan, nand_5_out, nand_6_out, nand_7_out);
  nand nand_12 (nand_12_out, nand_5_out, nand_6_out, nand_7_out, nand_10_out, nand_9_out, nand_8_out);
  nand nand_13 (lessthan, nand_8_out, nand_9_out, nand_10_out);
  nand nand_14 (areequal, nand_12_out, nand_12_out);

  // Other names for the same wires on the sheet: e = areequal; g = greaterthan; l = lessthan

  // Notes on the sheet:
  //   a1 a0
  //   b1 b0
  //   b1
  //   !b1
  //   !a1
  //   !b0
  //   b0
  //   14 NANDs solution
  //   !a0
  //   a1
  //   a0
  //   g =  a0 !b0 a1 + a0  !b0 !b1+ a1 !b1
  //   greater than circuit (from K-map)
  //   g
  //   equal to circuit
  //   l
  //   l =  b0 !a0 b1 + b0  !a0 !a1+ b1 !a1
  //   lesser than circuit (from K-map)
  //   e =  !g !l
endmodule
