// Logisim project 5_soln.circ as structural Verilog: 6 circuits, main circuit alu
module alu (
  input  [11:0] inputa,
  input  [11:0] inputb,
  input  [2:0] operation,
  output [11:0] aluout,
  output overflow,
  output carry,
  output zero
);

  wire addsub1_1_carry, addsub1_1_overflow, and_3_out;
  wire [1:0] or_2_out;
  wire [11:0] addsub1_1_out1, and1_1_andout, multiplexer_1_out, multiplexer_2_out, or1_1_orout, xor1_1_xorout;

  and and_1 (overflow, operation[2], addsub1_1_overflow);
  and and_2 (carry, operation[2], addsub1_1_carry);
  Multiplexer #(.width(12), .enable("false")) multiplexer_1 (
    .in0(inputb), .in1({12{1'b1}}), .out(multiplexer_1_out), .sel(operation[0]));
  Multiplexer #(.width(12), .enable("false")) multiplexer_2 (
    .in0(inputb), .in1(12'h1), .out(multiplexer_2_out), .sel(operation[1]));
  and and_3 (and_3_out, operation[0], ~operation[1]);  // AND_Gate
  or or_1 (or_2_out[1], operation[1], operation[2]);
  or or_2 (or_2_out[0], and_3_out, operation[2]);
  AND1 and1_1 (.inputa(inputa), .inputb(inputb), .andout(and1_1_andout));
  OR1 or1_1 (.inputa(inputa), .inputb(inputb), .orout(or1_1_orout));
  XOR1 xor1_1 (.inputa(inputa), .inputb(multiplexer_1_out), .xorout(xor1_1_xorout));
  ADDSUB1 addsub1_1 (
    .inputa(inputa), .inputb(multiplexer_2_out), .mode(operation[0]), .out1(addsub1_1_out1),
    .carry(addsub1_1_carry), .overflow(addsub1_1_overflow));
  Multiplexer #(.select(2), .width(12), .enable("false")) multiplexer_3 (
    .in0(and1_1_andout), .in1(or1_1_orout), .in2(xor1_1_xorout), .in3(addsub1_1_out1), .out(aluout),
    .sel(or_2_out));
  nor nor_1 (zero, aluout[11], aluout[10], aluout[9], aluout[8], aluout[7], aluout[6], aluout[5], aluout[4], aluout[3], aluout[2], aluout[1], aluout[0]);

  // Other names for the same wires on the sheet: alu[11:0] = aluout; z = zero

  // Notes on the sheet:
  //   mask
  //   f2
  //   f1
  //   f0
  //   s1 = f1 + f2
  //   s0 = f0 !f1 + f2
endmodule

module AND1 (
  input  [11:0] inputa,
  input  [11:0] inputb,
  output [11:0] andout
);

  assign andout = inputa & inputb;  // AND_Gate and_1, 12 bits wide
endmodule

module OR1 (
  input  [11:0] inputa,
  input  [11:0] inputb,
  output [11:0] orout
);

  assign orout = inputa | inputb;  // OR_Gate or_1, 12 bits wide
endmodule

module XOR1 (
  input  [11:0] inputa,
  input  [11:0] inputb,
  output [11:0] xorout
);

  assign xorout = inputa ^ inputb;  // XOR_Gate xor_1, 12 bits wide
endmodule

module ADD1 (
  input  [11:0] inputa,
  input  [11:0] inputb,
  input  carryin,
  output [11:0] sum,
  output overflow,
  output carry
);

  wire c_penult;
  wire [3:0] cla_1_carryout;
  wire [5:0] cla_1_propagator, cla_2_carryout, cla_2_propagator;

  xor xor_1 (overflow, c_penult, carry);
  cla cla_1 (
    .inputa(inputa[11:6]), .inputb(inputb[11:6]), .carryin(cla_2_carryout[5]),
    .carryout({carry, c_penult, cla_1_carryout}), .propagator(cla_1_propagator));  // open: generator
  cla cla_2 (
    .inputa(inputa[5:0]), .inputb(inputb[5:0]), .carryin(carryin), .carryout(cla_2_carryout),
    .propagator(cla_2_propagator));  // open: generator
  assign sum = {c_penult, cla_1_carryout, cla_2_carryout, carryin} ^ {cla_1_propagator, cla_2_propagator};  // XOR_Gate xor_2, 12 bits wide

  // Other names for the same wires on the sheet: c_last = carry; s[11:0] = sum

  // Notes on the sheet:
  //   carry
  //   propagator
endmodule

module ADDSUB1 (
  input  [11:0] inputa,
  input  [11:0] inputb,
  input  mode,
  output [11:0] out1,
  output carry,
  output overflow
);

  wire [11:0] xor_1_out;

  assign xor_1_out = inputb ^ {12{mode}};  // XOR_Gate xor_1, 12 bits wide
  ADD1 add1_1 (.inputa(inputa), .inputb(xor_1_out), .carryin(mode), .sum(out1), .overflow(overflow), .carry(carry));
endmodule
