// Logisim project 1_soln.circ as structural Verilog: 1 circuit, main circuit chaining
module chaining (
  input  q,
  input  sysclock,
  output q1ago,
  output q2ago
);

  D_Flip_Flop d_ff_1 (.D(q), .clk(sysclock), .Q(q1ago));  // open: Qn, preset, reset
  D_Flip_Flop d_ff_2 (.D(q1ago), .clk(sysclock), .Q(q2ago));  // open: Qn, preset, reset
endmodule
