// Logisim project 3_soln.circ as structural Verilog: 1 circuit, main circuit paritygen
module paritygen (
  input  inputw,
  input  sysclock,
  output outputq
);

  wire and_1_out, and_2_out, and_3_out, and_4_out, d_ff_1_q, d_ff_1_qn, d_ff_2_q, d_ff_2_qn, or_1_out,
       or_2_out;

  D_Flip_Flop d_ff_1 (.D(and_1_out), .clk(sysclock), .Q(d_ff_1_q), .Qn(d_ff_1_qn));  // open: preset, reset
  and and_1 (and_1_out, d_ff_2_qn, d_ff_1_qn);
  D_Flip_Flop d_ff_2 (.D(d_ff_1_q), .clk(sysclock), .Q(d_ff_2_q), .Qn(d_ff_2_qn));  // open: preset, reset
  or or_1 (or_1_out, d_ff_1_q, d_ff_2_q);
  and and_2 (and_2_out, or_1_out, outputq);
  and and_3 (and_3_out, ~inputw, and_2_out);  // AND_Gate
  or or_2 (or_2_out, and_3_out, and_4_out);
  and and_4 (and_4_out, inputw, ~and_2_out);  // AND_Gate
  D_Flip_Flop d_ff_3 (.D(or_2_out), .clk(sysclock), .Q(outputq));  // open: Qn, preset, reset

  // Other names for the same wires on the sheet: clk = sysclock; inp = inputw
endmodule
