// Logisim project 4_by_Lisa_Sun.circ as structural Verilog: 1 circuit, main circuit sequencecheck
module sequencecheck (
  input  inputx,
  input  sysclock,
  input  in_3,
  output outputr
);

  wire and_1_out, and_2_out, and_3_out, and_4_out, and_5_out, and_6_out, and_7_out, and_8_out, and_9_out, d0,
       d1, d2, q0, q0n, q1, q1n, q2, q2n, xn;

  not not_1 (xn, inputx);
  and and_1 (and_1_out, q1, q2n);
  and and_2 (and_2_out, q1n, q2);
  and and_3 (and_3_out, q2n, q0, inputx);
  and and_4 (and_4_out, xn, q1n);
  and and_5 (and_5_out, q1n, q2);
  and and_6 (and_6_out, q2n, q1, q0);
  and and_7 (and_7_out, xn, q0, q1n);
  and and_8 (and_8_out, q1, inputx, q2n);
  and and_9 (and_9_out, q2n, q0n, inputx);
  or or_1 (d2, and_1_out, and_2_out, and_3_out);
  or or_2 (d1, and_4_out, and_5_out, and_6_out);
  or or_3 (d0, and_7_out, and_8_out, and_9_out);
  and and_10 (outputr, q2, q0, q1, xn);
  D_Flip_Flop d_ff_1 (.D(d0), .clk(sysclock), .Q(q0), .Qn(q0n), .reset(in_3));  // open: preset
  D_Flip_Flop d_ff_2 (.D(d1), .clk(sysclock), .Q(q1), .Qn(q1n), .reset(in_3));  // open: preset
  D_Flip_Flop d_ff_3 (.D(d2), .clk(sysclock), .Q(q2), .Qn(q2n), .reset(in_3));  // open: preset

  // Other names for the same wires on the sheet: sc = sysclock; x = inputx; z = outputr

  // Notes on the sheet:
  //   This solution is by Lisa Sun
endmodule
