// Logisim project 4_soln.circ as structural Verilog: 1 circuit, main circuit sequencecheck
module sequencecheck (
  input  inputx,
  input  sysclock,
  output outputr
);

  wire and_2_out, and_3_out, d0, d1, d_ff_1_q, d_ff_1_qn, d_ff_2_q, d_ff_2_qn, d_ff_3_q, d_ff_3_qn, d_ff_4_q,
       or_1_out, or_2_out, or_3_out, or_4_out, q1_not, x_not;

  D_Flip_Flop d_ff_1 (.D(d_ff_2_qn), .clk(sysclock), .Q(d_ff_1_q), .Qn(d_ff_1_qn));  // open: preset, reset
  D_Flip_Flop d_ff_2 (.D(d_ff_1_q), .clk(sysclock), .Q(d_ff_2_q), .Qn(d_ff_2_qn));  // open: preset, reset
  D_Flip_Flop d_ff_3 (.D(d0), .clk(sysclock), .Q(d_ff_3_q), .Qn(d_ff_3_qn));  // open: preset, reset
  D_Flip_Flop d_ff_4 (.D(d1), .clk(sysclock), .Q(d_ff_4_q), .Qn(q1_not));  // open: preset, reset
  not not_1 (x_not, inputx);
  and and_1 (outputr, x_not, d_ff_1_qn, d_ff_2_q, q1_not);
  and and_2 (and_2_out, d_ff_1_qn, inputx);
  and and_3 (and_3_out, d_ff_1_q, d_ff_3_q);
  or or_1 (or_1_out, d_ff_2_q, d_ff_3_q, d_ff_4_q, x_not);
  or or_2 (or_2_out, d_ff_2_q, d_ff_3_qn, d_ff_4_q, inputx);
  or or_3 (or_3_out, d_ff_2_qn, d_ff_3_q, d_ff_4_q, inputx);
  or or_4 (or_4_out, d_ff_2_qn, d_ff_3_qn, d_ff_4_q, x_not);
  or or_5 (d0, and_2_out, and_3_out);
  and and_4 (d1, d_ff_1_q, or_1_out, or_2_out, or_3_out, or_4_out);

  // Other names for the same wires on the sheet: r = outputr; x = inputx

  // Notes on the sheet:
  //   q1 = 0 means sequence matched so far
  //   t0
  //   t1
  //   q0
  //   q1
  //   q0
  //   !q0
  //   !q1
  //   q1
  //   !x
  //   x
  //   t1
  //   !t1
  //   !t0
  //   t0
  //    First two FF's are to count time , time counts as: "00" -> "01" -> "11" -> "10" -> "00" ....
  //   r=1 iff time is just before reset,  sequence matched so far and input is "0"
  //   time is "10" means the last time before reset
  //   Let s be the sequence detected so far. Then states q1q0 are as follows:  
  //   for t="10",   "**" -> "**"
  //   for t="01",  q1q0 is : "00" when s=0,  01 when s=1
  //   for t="11",  q1q0 is : "00" when s="01",  is "01" when s="10", is "11" otherwise
  //   for t="10",  q1q0 is : "00" when s="010", is "01" when s="101", "11" otherwise
  //   state transition for q1q0 is given as: 
  //   for t="00",         "**" -0-> "00",      "**" -1-> "01" 
  //   for t="01",    "00" -0-> "1*",    "00" -1-> "00",    "01" -0-> "01",     "01" -1-> "1*",     "1*" -> "1*"
  //   for t="11",    "00" -0-> "00",    "00" -1-> "1*",    "01" -0-> "1*",     "01" -1-> "01",     "1*" -> "1*"
endmodule
