// Logisim project 1_soln.circ as structural Verilog: 4 circuits, main circuit alu8
module alu8 (
  input  [11:0] a,
  input  [11:0] b,
  input  [3:0] op,
  input  sysclock,
  output [11:0] alur
);

  wire ca, isaddsub, iscmp, ismsw, nand_1_out, nand_2_out, nand_3_out, ov, wensw;
  wire [0:0] nor_1_out, not_1_out;
  wire [1:1] or_1_out;
  wire [2:0] xor_2_out;
  wire [11:0] addsub1_1_out1, and_5_out, multiplexer_1_out, not_2_out, or_2_out, shifter_1_out,
       shifter_2_out, sw, xor_1_out;

  not not_1 (not_1_out[0], op[1]);
  or or_1 (or_1_out[1], op[1], op[3]);
  and and_1 (ismsw, op[0], op[1], op[2]);
  and and_2 (isaddsub, not_1_out[0], op[2], ~op[3]);  // AND_Gate
  and and_3 (iscmp, op[1], op[3]);
  nand nand_1 (nand_1_out, ~op[0], op[1]);  // NAND_Gate
  nand nand_2 (nand_2_out, op[1], op[2]);
  and and_4 (wensw, nand_2_out, nand_3_out);
  nand nand_3 (nand_3_out, ~op[2], op[3], nand_1_out);  // NAND_Gate
  assign not_2_out = ~a;  // NOT_Gate not_2, 12 bits wide
  assign and_5_out = a & b;  // AND_Gate and_5, 12 bits wide
  assign xor_1_out = a ^ b;  // XOR_Gate xor_1, 12 bits wide
  assign or_2_out = a | b;  // OR_Gate or_2, 12 bits wide
  Shifter #(.width(12)) shifter_1 (.in(a), .\dist ({3'b000, not_1_out[0]}), .out(shifter_1_out));
  Shifter #(.width(12), .shift("lr")) shifter_2 (.in(a), .\dist ({3'b000, not_1_out[0]}), .out(shifter_2_out));
  ADDSUB1 addsub1_1 (.inputa(a), .inputb(b), .mode(op[0]), .out1(addsub1_1_out1), .carry(ca), .overflow(ov));
  Multiplexer #(.select(3), .width(12), .enable("false")) multiplexer_1 (
    .in0(not_2_out), .in1(and_5_out), .in2(xor_1_out), .in3(or_2_out), .in4(addsub1_1_out1),
    .in5(addsub1_1_out1), .in6(shifter_1_out), .in7(shifter_2_out), .out(multiplexer_1_out),
    .sel({op[2], or_1_out[1], op[0]}));
  nor nor_1 (nor_1_out[0], multiplexer_1_out[11], multiplexer_1_out[10], multiplexer_1_out[9], multiplexer_1_out[8], multiplexer_1_out[7], multiplexer_1_out[6], multiplexer_1_out[5], multiplexer_1_out[4], multiplexer_1_out[3], multiplexer_1_out[2], multiplexer_1_out[1], multiplexer_1_out[0]);
  and and_6 (xor_2_out[1], ca, isaddsub);
  and and_7 (xor_2_out[2], ov, isaddsub);
  xor xor_2 (xor_2_out[0], nor_1_out[0], iscmp);
  Multiplexer #(.select(2), .width(12), .enable("false")) multiplexer_2 (
    .in0(multiplexer_1_out), .in1({{11{1'b0}}, nor_1_out[0]}), .in2(sw), .in3(sw), .out(alur),
    .sel({ismsw, iscmp}));
  Register #(.width(12)) register_1 (.D({{9{1'b0}}, xor_2_out}), .en(wensw), .clk(sysclock), .Q(sw));  // open: clr

  // Other names for the same wires on the sheet: clk = sysclock
endmodule

module ADD1 (
  input  [11:0] inputa,
  input  [11:0] inputb,
  input  carryin,
  output [11:0] sum,
  output overflow,
  output carry
);

  wire c_penult;
  wire [3:0] cla_1_carryout;
  wire [5:0] cla_1_propagator, cla_2_carryout, cla_2_propagator;

  xor xor_1 (overflow, c_penult, carry);
  cla cla_1 (
    .inputa(inputa[11:6]), .inputb(inputb[11:6]), .carryin(cla_2_carryout[5]),
    .carryout({carry, c_penult, cla_1_carryout}), .propagator(cla_1_propagator));  // open: generator
  cla cla_2 (
    .inputa(inputa[5:0]), .inputb(inputb[5:0]), .carryin(carryin), .carryout(cla_2_carryout),
    .propagator(cla_2_propagator));  // open: generator
  assign sum = {c_penult, cla_1_carryout, cla_2_carryout, carryin} ^ {cla_1_propagator, cla_2_propagator};  // XOR_Gate xor_2, 12 bits wide

  // Other names for the same wires on the sheet: c_last = carry; s[11:0] = sum

  // Notes on the sheet:
  //   carry
  //   propagator
endmodule

module ADDSUB1 (
  input  [11:0] inputa,
  input  [11:0] inputb,
  input  mode,
  output [11:0] out1,
  output carry,
  output overflow
);

  wire [11:0] xor_1_out;

  assign xor_1_out = inputb ^ {12{mode}};  // XOR_Gate xor_1, 12 bits wide
  ADD1 add1_1 (.inputa(inputa), .inputb(xor_1_out), .carryin(mode), .sum(out1), .overflow(overflow), .carry(carry));
endmodule

module cla (
  input  [5:0] inputa,
  input  [5:0] inputb,
  input  carryin,
  output [5:0] carryout,
  output [5:0] generator,
  output [5:0] propagator
);

  wire and_2_out, and_3_out, and_4_out, and_5_out, and_6_out, and_7_out, and_8_out, and_9_out, and_10_out,
       and_11_out, and_12_out, and_13_out, and_14_out, and_15_out, and_16_out, and_17_out, and_18_out,
       and_19_out, and_20_out, and_21_out, and_22_out;

  assign propagator = inputa ^ inputb;  // XOR_Gate xor_1, 6 bits wide
  assign generator = inputa & inputb;  // AND_Gate and_1, 6 bits wide
  and and_2 (and_2_out, carryin, propagator[0]);
  and and_3 (and_3_out, generator[0], propagator[1]);
  and and_4 (and_4_out, carryin, propagator[0], propagator[1]);
  and and_5 (and_5_out, generator[1], propagator[2]);
  and and_6 (and_6_out, generator[0], propagator[1], propagator[2]);
  and and_7 (and_7_out, carryin, propagator[0], propagator[1], propagator[2]);
  and and_8 (and_8_out, generator[2], propagator[3]);
  and and_9 (and_9_out, generator[1], propagator[2], propagator[3]);
  and and_10 (and_10_out, generator[0], propagator[1], propagator[2], propagator[3]);
  and and_11 (and_11_out, carryin, propagator[0], propagator[1], propagator[2], propagator[3]);
  and and_12 (and_12_out, generator[3], propagator[4]);
  and and_13 (and_13_out, generator[2], propagator[3], propagator[4]);
  and and_14 (and_14_out, generator[1], propagator[2], propagator[3], propagator[4]);
  and and_15 (and_15_out, generator[0], propagator[1], propagator[2], propagator[3], propagator[4]);
  and and_16 (and_16_out, carryin, propagator[0], propagator[1], propagator[2], propagator[3], propagator[4]);
  and and_17 (and_17_out, generator[4], propagator[5]);
  and and_18 (and_18_out, generator[3], propagator[4], propagator[5]);
  and and_19 (and_19_out, generator[2], propagator[3], propagator[4], propagator[5]);
  and and_20 (and_20_out, generator[1], propagator[2], propagator[3], propagator[4], propagator[5]);
  and and_21 (and_21_out, generator[0], propagator[1], propagator[2], propagator[3], propagator[4], propagator[5]);
  and and_22 (and_22_out, carryin, propagator[0], propagator[1], propagator[2], propagator[3], propagator[4], propagator[5]);
  or or_1 (carryout[0], and_2_out, generator[0]);
  or or_2 (carryout[1], generator[1], and_3_out, and_4_out);
  or or_3 (carryout[2], generator[2], and_5_out, and_6_out, and_7_out);
  or or_4 (carryout[3], generator[3], and_8_out, and_9_out, and_10_out, and_11_out);
  or or_5 (carryout[4], generator[4], and_12_out, and_13_out, and_14_out, and_15_out, and_16_out);
  or or_6 (carryout[5], generator[5], and_17_out, and_18_out, and_19_out, and_20_out, and_21_out, and_22_out);

  // Other names for the same wires on the sheet: cin = carryin; co[5:0] = carryout; p[5:0] = propagator

  // Notes on the sheet:
  //   a5 a4 a3 a2 a1 a0
  //   b5 b4 b3 b2 b1 b0
  //   g
  //   p
  //   g5 g4 g3 g2 g1 g0
  //   p5 p4 p3 p2 p1 p0
  //   cout1 = p1 p0 cin +p1 g0 + g1
  //   cout0 = p0 cin + g0
  //   cout2 = p2 p1 p0 cin + p2 p1 g0 + p2 g1 + g2
  //   cout3 = p3 p2 p1 p0 cin + p3 p2 p1 g0 + p3 p2 g1 + p3 g2 + g3
  //   cout4 = p4 p3 p2 p1 p0 cin + p4 p3 p2 p1 g0 + p4 p3 p2 g1 + p4 p3 g2 + p4 g3 + g4
  //   cout5 = p5 p4 p3 p2 p1 p0 cin + p5 p4 p3 p1 g0 + p5 p4 p3 p2 g1 + p5 p4 p3 g2 + p5 p4 g3 + p5 g4 + g5
endmodule
