// Logisim project 2_soln.circ as structural Verilog: 3 circuits, main circuit instructions
module instructions (
  input  resetall,
  input  sysclock,
  input  jmp,
  input  [11:0] a,
  output [11:0] pc,
  output [3:0] op,
  output [2:0] rd,
  output [2:0] rs1,
  output [2:0] rs2,
  output [11:0] imm
);

  wire and_1_out;
  wire [11:0] add1_1_sum, register_1_q;

  RAM #(.addrWidth(12), .dataWidth(25), .databus("bibus")) ram_1 (
    .addr(pc), .we(1'b0), .oe(1'b1), .clk(sysclock), .dout({op, rd, rs1, rs2, imm}));  // open: din
  ADD1 add1_1 (.inputa(pc), .inputb(12'h1), .sum(add1_1_sum));  // open: carryin, overflow, carry
  Register #(.width(12)) register_1 (.D(add1_1_sum), .en(1'b1), .clk(sysclock), .Q(register_1_q), .clr(resetall));
  Multiplexer #(.width(12), .enable("false")) multiplexer_1 (.in0(register_1_q), .in1(a), .out(pc), .sel(and_1_out));
  and and_1 (and_1_out, jmp, ~resetall);  // AND_Gate

  // Other names for the same wires on the sheet: clk = sysclock; rst = resetall
endmodule

module ADD1 (
  input  [11:0] inputa,
  input  [11:0] inputb,
  input  carryin,
  output [11:0] sum,
  output overflow,
  output carry
);

  wire c_penult;
  wire [3:0] cla_1_carryout;
  wire [5:0] cla_1_propagator, cla_2_carryout, cla_2_propagator;

  xor xor_1 (overflow, c_penult, carry);
  cla cla_1 (
    .inputa(inputa[11:6]), .inputb(inputb[11:6]), .carryin(cla_2_carryout[5]),
    .carryout({carry, c_penult, cla_1_carryout}), .propagator(cla_1_propagator));  // open: generator
  cla cla_2 (
    .inputa(inputa[5:0]), .inputb(inputb[5:0]), .carryin(carryin), .carryout(cla_2_carryout),
    .propagator(cla_2_propagator));  // open: generator
  assign sum = {c_penult, cla_1_carryout, cla_2_carryout, carryin} ^ {cla_1_propagator, cla_2_propagator};  // XOR_Gate xor_2, 12 bits wide

  // Other names for the same wires on the sheet: c_last = carry; s[11:0] = sum

  // Notes on the sheet:
  //   carry
  //   propagator
endmodule

module cla (
  input  [5:0] inputa,
  input  [5:0] inputb,
  input  carryin,
  output [5:0] carryout,
  output [5:0] generator,
  output [5:0] propagator
);

  wire and_2_out, and_3_out, and_4_out, and_5_out, and_6_out, and_7_out, and_8_out, and_9_out, and_10_out,
       and_11_out, and_12_out, and_13_out, and_14_out, and_15_out, and_16_out, and_17_out, and_18_out,
       and_19_out, and_20_out, and_21_out, and_22_out;

  assign propagator = inputa ^ inputb;  // XOR_Gate xor_1, 6 bits wide
  assign generator = inputa & inputb;  // AND_Gate and_1, 6 bits wide
  and and_2 (and_2_out, carryin, propagator[0]);
  and and_3 (and_3_out, generator[0], propagator[1]);
  and and_4 (and_4_out, carryin, propagator[0], propagator[1]);
  and and_5 (and_5_out, generator[1], propagator[2]);
  and and_6 (and_6_out, generator[0], propagator[1], propagator[2]);
  and and_7 (and_7_out, carryin, propagator[0], propagator[1], propagator[2]);
  and and_8 (and_8_out, generator[2], propagator[3]);
  and and_9 (and_9_out, generator[1], propagator[2], propagator[3]);
  and and_10 (and_10_out, generator[0], propagator[1], propagator[2], propagator[3]);
  and and_11 (and_11_out, carryin, propagator[0], propagator[1], propagator[2], propagator[3]);
  and and_12 (and_12_out, generator[3], propagator[4]);
  and and_13 (and_13_out, generator[2], propagator[3], propagator[4]);
  and and_14 (and_14_out, generator[1], propagator[2], propagator[3], propagator[4]);
  and and_15 (and_15_out, generator[0], propagator[1], propagator[2], propagator[3], propagator[4]);
  and and_16 (and_16_out, carryin, propagator[0], propagator[1], propagator[2], propagator[3], propagator[4]);
  and and_17 (and_17_out, generator[4], propagator[5]);
  and and_18 (and_18_out, generator[3], propagator[4], propagator[5]);
  and and_19 (and_19_out, generator[2], propagator[3], propagator[4], propagator[5]);
  and and_20 (and_20_out, generator[1], propagator[2], propagator[3], propagator[4], propagator[5]);
  and and_21 (and_21_out, generator[0], propagator[1], propagator[2], propagator[3], propagator[4], propagator[5]);
  and and_22 (and_22_out, carryin, propagator[0], propagator[1], propagator[2], propagator[3], propagator[4], propagator[5]);
  or or_1 (carryout[0], and_2_out, generator[0]);
  or or_2 (carryout[1], generator[1], and_3_out, and_4_out);
  or or_3 (carryout[2], generator[2], and_5_out, and_6_out, and_7_out);
  or or_4 (carryout[3], generator[3], and_8_out, and_9_out, and_10_out, and_11_out);
  or or_5 (carryout[4], generator[4], and_12_out, and_13_out, and_14_out, and_15_out, and_16_out);
  or or_6 (carryout[5], generator[5], and_17_out, and_18_out, and_19_out, and_20_out, and_21_out, and_22_out);

  // Other names for the same wires on the sheet: cin = carryin; co[5:0] = carryout; p[5:0] = propagator

  // Notes on the sheet:
  //   a5 a4 a3 a2 a1 a0
  //   b5 b4 b3 b2 b1 b0
  //   g
  //   p
  //   g5 g4 g3 g2 g1 g0
  //   p5 p4 p3 p2 p1 p0
  //   cout1 = p1 p0 cin +p1 g0 + g1
  //   cout0 = p0 cin + g0
  //   cout2 = p2 p1 p0 cin + p2 p1 g0 + p2 g1 + g2
  //   cout3 = p3 p2 p1 p0 cin + p3 p2 p1 g0 + p3 p2 g1 + p3 g2 + g3
  //   cout4 = p4 p3 p2 p1 p0 cin + p4 p3 p2 p1 g0 + p4 p3 p2 g1 + p4 p3 g2 + p4 g3 + g4
  //   cout5 = p5 p4 p3 p2 p1 p0 cin + p5 p4 p3 p1 g0 + p5 p4 p3 p2 g1 + p5 p4 p3 g2 + p5 p4 g3 + p5 g4 + g5
endmodule
